// Logisim project Muhammad_Bilal_(33405).circ as structural Verilog
module Add_1_V1 (
  input  A,
  input  B,
  input  Carry_In,
  output Sum_out,
  output Carry_Out
);

  wire and_1_out, and_2_out, xor_1_out;

  xor xor_1 (xor_1_out, A, B);
  and and_1 (and_1_out, A, B);
  xor xor_2 (Sum_out, xor_1_out, Carry_In);
  and and_2 (and_2_out, xor_1_out, Carry_In);
  or or_1 (Carry_Out, and_2_out, and_1_out);
endmodule

module Add_2_V1 (
  input  [1:0] A,
  input  [1:0] B,
  input  Carry_In,
  output [1:0] Sum_out,
  output Carry_out
);

  wire add_1_v1_1_carry_out;

  // Probe on A
  // Probe on B
  Add_1_V1 add_1_v1_1 (.A(A[0]), .B(B[0]), .Carry_In(Carry_In), .Sum_out(Sum_out[0]), .Carry_Out(add_1_v1_1_carry_out));
  Add_1_V1 add_1_v1_2 (
    .A(A[1]), .B(B[1]), .Carry_In(add_1_v1_1_carry_out), .Sum_out(Sum_out[1]), .Carry_Out(Carry_out));
  // Probe on Sum_out
endmodule

module Add_4_V1 (
  input  [3:0] A,
  input  [3:0] B,
  input  Carry_In,
  output [3:0] Sum_out,
  output Carry_out
);

  wire add_2_v1_1_carry_out;

  // Probe on B
  // Probe on A
  Add_2_V1 add_2_v1_1 (
    .A(A[1:0]), .B(B[1:0]), .Carry_In(Carry_In), .Sum_out(Sum_out[1:0]), .Carry_out(add_2_v1_1_carry_out));
  Add_2_V1 add_2_v1_2 (
    .A(A[3:2]), .B(B[3:2]), .Carry_In(add_2_v1_1_carry_out), .Sum_out(Sum_out[3:2]), .Carry_out(Carry_out));
  // Probe on Sum_out
endmodule

module Add_8_V1 (
  input  [7:0] A,
  input  [7:0] B,
  input  Carry_In,
  output [7:0] Sum_out,
  output Carry_Out
);

  wire add_4_v1_1_carry_out;

  // Probe on A
  // Probe on B
  Add_4_V1 add_4_v1_1 (
    .A(A[3:0]), .B(B[3:0]), .Carry_In(Carry_In), .Sum_out(Sum_out[3:0]), .Carry_out(add_4_v1_1_carry_out));
  Add_4_V1 add_4_v1_2 (
    .A(A[7:4]), .B(B[7:4]), .Carry_In(add_4_v1_1_carry_out), .Sum_out(Sum_out[7:4]), .Carry_out(Carry_Out));
  // Probe on Sum_out
endmodule

module Add_16_V1 (
  input  [15:0] A,
  input  [15:0] B,
  input  Carry_In,
  output [15:0] Sum_out,
  output Carry_Out
);

  wire add_8_v1_1_carry_out;

  // Probe on A
  // Probe on B
  Add_8_V1 add_8_v1_1 (
    .A(A[7:0]), .B(B[7:0]), .Carry_In(Carry_In), .Sum_out(Sum_out[7:0]), .Carry_Out(add_8_v1_1_carry_out));
  Add_8_V1 add_8_v1_2 (
    .A(A[15:8]), .B(B[15:8]), .Carry_In(add_8_v1_1_carry_out), .Sum_out(Sum_out[15:8]), .Carry_Out(Carry_Out));
  // Probe on Sum_out
endmodule

module Add_32_V1 (
  input  [31:0] A,
  input  [31:0] B,
  input  Carry_In,
  output [31:0] Sum_out,
  output Carry_Out
);

  wire add_16_v1_1_carry_out;

  // Probe on A
  // Probe on B
  Add_16_V1 add_16_v1_1 (
    .A(A[15:0]), .B(B[15:0]), .Carry_In(Carry_In), .Sum_out(Sum_out[15:0]), .Carry_Out(add_16_v1_1_carry_out));
  Add_16_V1 add_16_v1_2 (
    .A(A[31:16]), .B(B[31:16]), .Carry_In(add_16_v1_1_carry_out), .Sum_out(Sum_out[31:16]),
    .Carry_Out(Carry_Out));
  // Probe on Sum_out
endmodule

module Add_64_V1 (
  input  [63:0] A,
  input  [63:0] B,
  input  Carry_In,
  output [63:0] Sum_out,
  output Carry_Out
);

  wire add_32_v1_1_carry_out;

  Add_32_V1 add_32_v1_1 (
    .A(A[31:0]), .B(B[31:0]), .Carry_In(Carry_In), .Sum_out(Sum_out[31:0]), .Carry_Out(add_32_v1_1_carry_out));
  Add_32_V1 add_32_v1_2 (
    .A(A[63:32]), .B(B[63:32]), .Carry_In(add_32_v1_1_carry_out), .Sum_out(Sum_out[63:32]),
    .Carry_Out(Carry_Out));
endmodule

module Data_Flow (
);

  wire clock_1_out, or_2_out;
  wire [7:0] counter_1_q, counter_3_q, counter_4_q;
  wire [15:0] controlled_buffer_1_out, core_multi_1_sum1, core_multi_1_sum2, core_multi_1_sum_3,
       core_multi_1_sum_4, ram_1_dout, ram_2_dout, register_1_q, register_2_q, register_3_q, register_4_q,
       register_5_q, register_6_q, register_7_q, register_8_q, register_9_q, register_10_q, register_11_q,
       register_12_q, rom_1_data;

  // OR_Gate or_1 has open pins: in0=rom_1_data[4], in1=rom_1_data[5], in2=rom_1_data[6], in3=rom_1_data[7], out=open
  Counter counter_1 (.Q(counter_1_q), .up(1'b1), .clk(clock_1_out));  // open: load, D, count, carry, clr
  RAM #(.dataWidth(16), .\type ("nonvolatile")) ram_1 (
    .addr(counter_1_q), .clk(clock_1_out), .dout(ram_1_dout));  // open: we, oe, din
  Register #(.width(16)) register_1 (
    .D(ram_1_dout), .en(rom_1_data[0]), .clk(clock_1_out), .Q(register_1_q));  // open: clr
  Register #(.width(16)) register_2 (
    .D(ram_1_dout), .en(rom_1_data[1]), .clk(clock_1_out), .Q(register_2_q));  // open: clr
  Register #(.width(16)) register_3 (
    .D(ram_1_dout), .en(rom_1_data[2]), .clk(clock_1_out), .Q(register_3_q));  // open: clr
  Register #(.width(16)) register_4 (
    .D(ram_1_dout), .en(rom_1_data[3]), .clk(clock_1_out), .Q(register_4_q));  // open: clr
  RAM #(.dataWidth(16), .\type ("nonvolatile")) ram_2 (
    .addr(counter_1_q), .clk(clock_1_out), .dout(ram_2_dout));  // open: we, oe, din
  Register #(.width(16)) register_5 (
    .D(ram_2_dout), .en(rom_1_data[4]), .clk(clock_1_out), .Q(register_5_q));  // open: clr
  Register #(.width(16)) register_6 (
    .D(ram_2_dout), .en(rom_1_data[5]), .clk(clock_1_out), .Q(register_6_q));  // open: clr
  Register #(.width(16)) register_7 (
    .D(ram_2_dout), .en(rom_1_data[6]), .clk(clock_1_out), .Q(register_7_q));  // open: clr
  Register #(.width(16)) register_8 (
    .D(ram_2_dout), .en(rom_1_data[7]), .clk(clock_1_out), .Q(register_8_q));  // open: clr
  Clock clock_1 (.out(clock_1_out));
  Counter #(.max('hffff), .width(16)) counter_2 ();  // open: load, D, count, Q, carry, up, clk, clr
  core_multi core_multi_1 (
    .A(register_1_q), .A1(register_2_q), .B(register_5_q), .B1(register_6_q), .A2(register_3_q),
    .B2(register_7_q), .A3(register_4_q), .B3(register_8_q), .sum1(core_multi_1_sum1),
    .sum2(core_multi_1_sum2), .sum_3(core_multi_1_sum_3), .sum_4(core_multi_1_sum_4));  // open: cout1, cout2, cout3, cout4
  Register #(.width(16)) register_9 (
    .D(core_multi_1_sum1), .en(rom_1_data[8]), .clk(clock_1_out), .Q(register_9_q));  // open: clr
  Register #(.width(16)) register_10 (
    .D(core_multi_1_sum2), .en(rom_1_data[9]), .clk(clock_1_out), .Q(register_10_q));  // open: clr
  Register #(.width(16)) register_11 (
    .D(core_multi_1_sum_3), .en(rom_1_data[10]), .clk(clock_1_out), .Q(register_11_q));  // open: clr
  Register #(.width(16)) register_12 (
    .D(core_multi_1_sum_4), .en(rom_1_data[11]), .clk(clock_1_out), .Q(register_12_q));  // open: clr
  assign controlled_buffer_1_out = rom_1_data[12] ? register_9_q : 16'bz;  // Controlled_Buffer controlled_buffer_1
  assign controlled_buffer_1_out = rom_1_data[13] ? register_10_q : 16'bz;  // Controlled_Buffer controlled_buffer_2
  assign controlled_buffer_1_out = rom_1_data[14] ? register_11_q : 16'bz;  // Controlled_Buffer controlled_buffer_3
  assign controlled_buffer_1_out = rom_1_data[15] ? register_12_q : 16'bz;  // Controlled_Buffer controlled_buffer_4
  Counter counter_3 (.Q(counter_3_q), .clk(clock_1_out));  // open: load, D, count, carry, up, clr
  or or_2 (or_2_out, rom_1_data[12], rom_1_data[13], rom_1_data[14], rom_1_data[15]);
  ROM #(.dataWidth(16)) rom_1 (.addr(counter_3_q), .data(rom_1_data));
  RAM #(.dataWidth(16)) ram_3 (
    .addr(counter_4_q), .we(clock_1_out), .clk(clock_1_out), .din(controlled_buffer_1_out));  // open: oe, dout
  Counter counter_4 (.count(or_2_out), .Q(counter_4_q), .clk(clock_1_out));  // open: load, D, carry, up, clr
  RAM #(.dataWidth(16), .\type ("nonvolatile")) ram_4 (.addr(counter_4_q));  // open: we, oe, clk, din, dout
  Hex_Digit_Display hex_digit_display_1 (.value(counter_3_q[7:4]));  // open: dp
  Hex_Digit_Display hex_digit_display_2 (.value(counter_3_q[3:0]));  // open: dp

  // Notes on the sheet:
  //   contents of rom_1 (hex, n*v repeats v):
  //   0 11 122 1244 2488 4811 8122 1244 2488 4811 8122 1244 2488 4811 8122 1244 2488 4811 8122 1244 2488
  //   4811 8122 1244 2488 4811 8122 1244 2488 4811 8122 1244 2488 4811 8122 1244 2488 4811 8122 1244 2488
  //   4811 8122 1244 2488 4811 8122 1244 2488 4811 8122 1244 2488 4811 8122 1244 2488 4811 8122 1244 2488
  //   4811 8122 1244 2488 4811 8122 1244 2488 4811 8122 1244
endmodule

module core_multi (
  input  [15:0] A,
  input  [15:0] A1,
  input  [15:0] B,
  input  [15:0] B1,
  input  [15:0] A2,
  input  [15:0] B2,
  input  [15:0] A3,
  input  [15:0] B3,
  output [15:0] sum1,
  output cout1,
  output [15:0] sum2,
  output cout2,
  output [15:0] sum_3,
  output cout3,
  output [15:0] sum_4,
  output cout4
);

  Add_16_V1 add_16_v1_1 (.A(A), .B(B), .Sum_out(sum1), .Carry_Out(cout1));  // open: Carry_In
  Add_16_V1 add_16_v1_2 (.A(A2), .B(B2), .Sum_out(sum_3), .Carry_Out(cout3));  // open: Carry_In
  Add_16_V1 add_16_v1_3 (.A(A3), .B(B3), .Sum_out(sum_4), .Carry_Out(cout4));  // open: Carry_In
  Add_16_V1 add_16_v1_4 (.A(A1), .B(B1), .Sum_out(sum2), .Carry_Out(cout2));  // open: Carry_In
endmodule

module matmul (
  input  [15:0] A,
  input  [15:0] A1,
  input  [15:0] B,
  input  [15:0] B1,
  input  [15:0] A2,
  input  [15:0] B2,
  input  [15:0] A3,
  input  [15:0] B3,
  output [15:0] sum2
);

  wire [15:0] adder_1_out, adder_2_out, multiplier_1_out, multiplier_2_out, multiplier_3_out,
       multiplier_4_out;

  Multiplier #(.width(16)) multiplier_1 (.a(A), .b(B), .out(multiplier_1_out));  // open: cin, cout
  Multiplier #(.width(16)) multiplier_2 (.a(A2), .b(B2), .out(multiplier_2_out));  // open: cin, cout
  Multiplier #(.width(16)) multiplier_3 (.a(A3), .b(B3), .out(multiplier_3_out));  // open: cin, cout
  Multiplier #(.width(16)) multiplier_4 (.a(A1), .b(B1), .out(multiplier_4_out));  // open: cin, cout
  Adder #(.width(16)) adder_1 (.a(multiplier_2_out), .b(multiplier_3_out), .out(adder_1_out));  // open: cin, cout
  Adder #(.width(16)) adder_2 (.a(multiplier_1_out), .b(multiplier_4_out), .out(adder_2_out));  // open: cin, cout
  Adder #(.width(16)) adder_3 (.a(adder_2_out), .b(adder_1_out), .out(sum2));  // open: cin, cout
endmodule

module Matmul_trying (
);

  wire clock_1_out, or_1_out, or_2_out;
  wire [7:0] counter_1_q, counter_2_q, counter_3_q, counter_4_q;
  wire [15:0] matmul_1_sum2, ram_1_dout, ram_2_dout, register_1_q, register_2_q, register_3_q, register_4_q,
       register_5_q, register_6_q, register_7_q, register_8_q, register_9_q, rom_1_data;

  or or_1 (or_1_out, rom_1_data[0], rom_1_data[1], rom_1_data[2], rom_1_data[3]);
  or or_2 (or_2_out, rom_1_data[4], rom_1_data[5], rom_1_data[6], rom_1_data[7]);
  Counter #(.max('h4)) counter_1 (
    .count(or_2_out), .Q(counter_1_q), .up(1'b1), .clk(clock_1_out));  // open: load, D, carry, clr
  RAM #(.dataWidth(16), .\type ("nonvolatile")) ram_1 (
    .addr(counter_1_q), .clk(clock_1_out), .dout(ram_1_dout));  // open: we, oe, din
  Register #(.width(16)) register_1 (
    .D(ram_1_dout), .en(rom_1_data[0]), .clk(clock_1_out), .Q(register_1_q));  // open: clr
  Register #(.width(16)) register_2 (
    .D(ram_1_dout), .en(rom_1_data[1]), .clk(clock_1_out), .Q(register_2_q));  // open: clr
  Register #(.width(16)) register_3 (
    .D(ram_1_dout), .en(rom_1_data[2]), .clk(clock_1_out), .Q(register_3_q));  // open: clr
  Register #(.width(16)) register_4 (
    .D(ram_1_dout), .en(rom_1_data[3]), .clk(clock_1_out), .Q(register_4_q));  // open: clr
  Counter counter_2 (.count(or_1_out), .Q(counter_2_q), .up(1'b1), .clk(clock_1_out));  // open: load, D, carry, clr
  RAM #(.dataWidth(16), .\type ("nonvolatile")) ram_2 (
    .addr(counter_2_q), .oe(clock_1_out), .clk(clock_1_out), .dout(ram_2_dout));  // open: we, din
  Register #(.width(16)) register_5 (
    .D(ram_2_dout), .en(rom_1_data[4]), .clk(clock_1_out), .Q(register_5_q));  // open: clr
  Register #(.width(16)) register_6 (
    .D(ram_2_dout), .en(rom_1_data[5]), .clk(clock_1_out), .Q(register_6_q));  // open: clr
  Register #(.width(16)) register_7 (
    .D(ram_2_dout), .en(rom_1_data[6]), .clk(clock_1_out), .Q(register_7_q));  // open: clr
  Register #(.width(16)) register_8 (
    .D(ram_2_dout), .en(rom_1_data[7]), .clk(clock_1_out), .Q(register_8_q));  // open: clr
  Clock clock_1 (.out(clock_1_out));
  matmul matmul_1 (
    .A(register_1_q), .A1(register_2_q), .B(register_5_q), .B1(register_6_q), .A2(register_3_q),
    .B2(register_7_q), .A3(register_4_q), .B3(register_8_q), .sum2(matmul_1_sum2));
  Register #(.width(16)) register_9 (
    .D(matmul_1_sum2), .en(rom_1_data[8]), .clk(clock_1_out), .Q(register_9_q));  // open: clr
  Counter counter_3 (.count(clock_1_out), .Q(counter_3_q), .clk(clock_1_out));  // open: load, D, carry, up, clr
  Counter counter_4 (.Q(counter_4_q), .clk(clock_1_out));  // open: load, D, count, carry, up, clr
  ROM #(.dataWidth(16)) rom_1 (.addr(counter_4_q), .data(rom_1_data));
  RAM #(.dataWidth(16), .\type ("nonvolatile")) ram_3 (.addr(counter_3_q));  // open: we, oe, clk, din, dout
  RAM #(.dataWidth(16)) ram_4 (
    .addr(counter_3_q), .we(clock_1_out), .clk(clock_1_out), .din(register_9_q));  // open: oe, dout
  Hex_Digit_Display hex_digit_display_1 (.value(counter_4_q[7:4]));  // open: dp
  Hex_Digit_Display hex_digit_display_2 (.value(counter_4_q[3:0]));  // open: dp

  // Notes on the sheet:
  //   contents of rom_1 (hex, n*v repeats v):
  //   0 11 122 1244 2488 4811 8122 1244 2488 4811 8122 1244 2488 4811 8122 1244 2488 4811 8122 1244 2488
  //   4811 8122 1244 2488 4811 8122 1244 2488 4811 8122 1244 2488 4811 8122 1244 2488 4811 8122 1244 2488
  //   4811 8122 1244 2488 4811 8122 1244 2488 4811 8122 1244 2488 4811 8122 1244 2488 4811 8122 1244 2488
  //   4811 8122 1244 2488 4811 8122 1244 2488 4811 8122 1244
endmodule

module strassen_tiling (
);

  wire clock_1_out, clock_2_out, or_1_out, or_2_out, or_3_out, or_4_out, or_5_out;
  wire [3:0] counter_5_q, counter_5_q_2;
  wire [7:0] counter_1_q, counter_2_q, counter_3_q, counter_4_q, counter_6_q;
  wire [15:0] adder_2x2_1_out_9, adder_2x2_1_out_10, adder_2x2_1_out_11, adder_2x2_1_out_12,
       controlled_buffer_1_out, core2x2_1_a, core2x2_1_b, core2x2_1_c, core2x2_1_d, core2x2_2_a, core2x2_2_b,
       core2x2_2_c, core2x2_2_d, ram_1_dout, ram_2_dout, ram_3_dout, ram_4_dout, register_1_q, register_2_q,
       register_3_q, register_4_q, register_5_q, register_6_q, register_7_q, register_8_q, register_9_q,
       register_10_q, register_11_q, register_12_q, register_13_q, register_14_q, register_15_q,
       register_16_q, register_17_q, register_18_q, register_19_q, register_20_q;
  wire [23:0] rom_1_data;

  or or_1 (or_1_out, rom_1_data[3], rom_1_data[2], rom_1_data[1], rom_1_data[0]);
  Counter counter_1 (.count(or_1_out), .Q(counter_1_q), .up(1'b1), .clk(clock_1_out));  // open: load, D, carry, clr
  Clock clock_1 (.out(clock_1_out));
  RAM #(.dataWidth(16), .\type ("nonvolatile")) ram_1 (
    .addr(counter_1_q), .clk(clock_1_out), .dout(ram_1_dout));  // open: we, oe, din
  or or_2 (or_2_out, rom_1_data[7], rom_1_data[6], rom_1_data[5], rom_1_data[4]);
  Register #(.width(16)) register_1 (
    .D(ram_1_dout), .en(rom_1_data[0]), .clk(clock_1_out), .Q(register_1_q));  // open: clr
  Register #(.width(16)) register_2 (
    .D(ram_1_dout), .en(rom_1_data[1]), .clk(clock_1_out), .Q(register_2_q));  // open: clr
  Register #(.width(16)) register_3 (
    .D(ram_1_dout), .en(rom_1_data[2]), .clk(clock_1_out), .Q(register_3_q));  // open: clr
  Register #(.width(16)) register_4 (
    .D(ram_1_dout), .en(rom_1_data[3]), .clk(clock_1_out), .Q(register_4_q));  // open: clr
  Counter #(.max('h7)) counter_2 (
    .count(or_2_out), .Q(counter_2_q), .up(1'b1), .clk(clock_1_out));  // open: load, D, carry, clr
  RAM #(.dataWidth(16), .\type ("nonvolatile")) ram_2 (
    .addr(counter_2_q), .clk(clock_1_out), .dout(ram_2_dout));  // open: we, oe, din
  Register #(.width(16)) register_5 (
    .D(ram_2_dout), .en(rom_1_data[4]), .clk(clock_1_out), .Q(register_5_q));  // open: clr
  Register #(.width(16)) register_6 (
    .D(ram_2_dout), .en(rom_1_data[5]), .clk(clock_1_out), .Q(register_6_q));  // open: clr
  Register #(.width(16)) register_7 (
    .D(ram_2_dout), .en(rom_1_data[6]), .clk(clock_1_out), .Q(register_7_q));  // open: clr
  Register #(.width(16)) register_8 (
    .D(ram_2_dout), .en(rom_1_data[7]), .clk(clock_1_out), .Q(register_8_q));  // open: clr
  Counter counter_3 (.count(or_3_out), .Q(counter_3_q), .up(1'b1), .clk(clock_1_out));  // open: load, D, carry, clr
  or or_3 (or_3_out, rom_1_data[11], rom_1_data[10], rom_1_data[9], rom_1_data[8]);
  RAM #(.dataWidth(16), .\type ("nonvolatile")) ram_3 (
    .addr(counter_3_q), .clk(clock_1_out), .dout(ram_3_dout));  // open: we, oe, din
  Register #(.width(16)) register_9 (
    .D(ram_3_dout), .en(rom_1_data[8]), .clk(clock_1_out), .Q(register_9_q));  // open: clr
  Register #(.width(16)) register_10 (
    .D(ram_3_dout), .en(rom_1_data[9]), .clk(clock_1_out), .Q(register_10_q));  // open: clr
  Register #(.width(16)) register_11 (
    .D(ram_3_dout), .en(rom_1_data[10]), .clk(clock_1_out), .Q(register_11_q));  // open: clr
  Register #(.width(16)) register_12 (
    .D(ram_3_dout), .en(rom_1_data[11]), .clk(clock_1_out), .Q(register_12_q));  // open: clr
  Counter #(.max('h7)) counter_4 (
    .count(or_4_out), .Q(counter_4_q), .up(1'b1), .clk(clock_1_out));  // open: load, D, carry, clr
  or or_4 (or_4_out, rom_1_data[15], rom_1_data[14], rom_1_data[13], rom_1_data[12]);
  RAM #(.dataWidth(16), .\type ("nonvolatile")) ram_4 (
    .addr(counter_4_q), .clk(clock_1_out), .dout(ram_4_dout));  // open: we, oe, din
  Register #(.width(16)) register_13 (
    .D(ram_4_dout), .en(rom_1_data[12]), .clk(clock_1_out), .Q(register_13_q));  // open: clr
  Register #(.width(16)) register_14 (
    .D(ram_4_dout), .en(rom_1_data[14]), .clk(clock_1_out), .Q(register_14_q));  // open: clr
  Register #(.width(16)) register_15 (
    .D(ram_4_dout), .en(rom_1_data[15]), .clk(clock_1_out), .Q(register_15_q));  // open: clr
  Register #(.width(16)) register_16 (
    .D(ram_4_dout), .en(rom_1_data[13]), .clk(clock_1_out), .Q(register_16_q));  // open: clr
  core2x2 core2x2_1 (
    .A1(register_1_q), .A2(register_2_q), .A3(register_3_q), .A4(register_4_q), .B1(register_5_q),
    .B2(register_6_q), .B3(register_7_q), .B4(register_8_q), .A(core2x2_1_a), .B(core2x2_1_b),
    .C(core2x2_1_c), .D(core2x2_1_d));
  core2x2 core2x2_2 (
    .A1(register_9_q), .A2(register_10_q), .A3(register_11_q), .A4(register_12_q), .B1(register_13_q),
    .B2(register_16_q), .B3(register_14_q), .B4(register_15_q), .A(core2x2_2_a), .B(core2x2_2_b),
    .C(core2x2_2_c), .D(core2x2_2_d));
  Clock clock_2 (.out(clock_2_out));
  Adder_2x2 adder_2x2_1 (
    .A(core2x2_1_a), .A1(core2x2_2_a), .B(core2x2_1_b), .B1(core2x2_2_b), .C(core2x2_1_c), .C1(core2x2_2_c),
    .D(core2x2_1_d), .D1(core2x2_2_d), .out_9(adder_2x2_1_out_9), .out_10(adder_2x2_1_out_10),
    .out_11(adder_2x2_1_out_11), .out_12(adder_2x2_1_out_12));
  Register #(.width(16)) register_17 (
    .D(adder_2x2_1_out_9), .en(rom_1_data[16]), .clk(clock_2_out), .Q(register_17_q));  // open: clr
  Register #(.width(16)) register_18 (
    .D(adder_2x2_1_out_10), .en(rom_1_data[16]), .clk(clock_2_out), .Q(register_18_q));  // open: clr
  Register #(.width(16)) register_19 (
    .D(adder_2x2_1_out_11), .en(rom_1_data[16]), .clk(clock_2_out), .Q(register_19_q));  // open: clr
  Register #(.width(16)) register_20 (
    .D(adder_2x2_1_out_12), .en(rom_1_data[16]), .clk(clock_2_out), .Q(register_20_q));  // open: clr
  assign controlled_buffer_1_out = rom_1_data[20] ? register_17_q : 16'bz;  // Controlled_Buffer controlled_buffer_1
  assign controlled_buffer_1_out = rom_1_data[21] ? register_18_q : 16'bz;  // Controlled_Buffer controlled_buffer_2
  assign controlled_buffer_1_out = rom_1_data[22] ? register_19_q : 16'bz;  // Controlled_Buffer controlled_buffer_3
  assign controlled_buffer_1_out = rom_1_data[23] ? register_20_q : 16'bz;  // Controlled_Buffer controlled_buffer_4
  Counter counter_5 (
    .Q({counter_5_q_2, counter_5_q}), .up(1'b1), .clk(clock_2_out));  // open: load, D, count, carry, clr
  ROM #(.dataWidth(24)) rom_1 (.addr({counter_5_q_2, counter_5_q}), .data(rom_1_data));
  Counter counter_6 (.count(or_5_out), .Q(counter_6_q), .up(1'b1), .clk(clock_2_out));  // open: load, D, carry, clr
  or or_5 (or_5_out, rom_1_data[20], rom_1_data[21], rom_1_data[22], rom_1_data[23]);
  RAM #(.dataWidth(16)) ram_5 (
    .addr(counter_6_q), .we(or_5_out), .clk(clock_2_out), .din(controlled_buffer_1_out));  // open: oe, dout
  RAM #(.dataWidth(16)) ram_6 (.addr(counter_6_q));  // open: we, oe, clk, din, dout
  Hex_Digit_Display hex_digit_display_1 (.value(counter_5_q_2));  // open: dp
  Hex_Digit_Display hex_digit_display_2 (.value(counter_5_q));  // open: dp
  // Probe on {counter_5_q_2, counter_5_q}

  // Notes on the sheet:
  //   contents of rom_1 (hex, n*v repeats v):
  //   1111 1111 2222 4444 8888 11010 102020 204040 408080 800000 11111 102222 204444 408888 811010 102020
  //   204040 408080 800000 10000 100000 200000 400000 800000
endmodule

module systollic (
  input  [15:0] sumIN,
  input  [15:0] A,
  input  [15:0] B,
  input  we,
  output [15:0] SUm_out,
  output [15:0] Aout,
  output [15:0] bout
);

  wire clock_1_out;
  wire [15:0] adder_1_out, multiplier_1_out;

  Clock clock_1 (.out(clock_1_out));
  Multiplier #(.width(16)) multiplier_1 (.a(A), .b(B), .out(multiplier_1_out));  // open: cin, cout
  Register #(.width(16)) register_1 (.D(A), .clk(clock_1_out), .Q(Aout));  // open: en, clr
  Adder #(.width(16)) adder_1 (.a(sumIN), .b(multiplier_1_out), .out(adder_1_out));  // open: cin, cout
  Register #(.width(16)) register_2 (.D(B), .clk(clock_1_out), .Q(bout));  // open: en, clr
  Register #(.width(16)) register_3 (.D(adder_1_out), .en(we), .clk(clock_1_out), .Q(SUm_out));  // open: clr
endmodule

module core2x2 (
  input  [15:0] A1,
  input  [15:0] A2,
  input  [15:0] A3,
  input  [15:0] A4,
  input  [15:0] B1,
  input  [15:0] B2,
  input  [15:0] B3,
  input  [15:0] B4,
  output [15:0] A,
  output [15:0] B,
  output [15:0] C,
  output [15:0] D
);

  wire [15:0] multiplier_1_out, multiplier_2_out, multiplier_3_out, multiplier_4_out, multiplier_5_out,
       multiplier_6_out, multiplier_7_out, multiplier_8_out;

  Multiplier #(.width(16)) multiplier_1 (.a(A1), .b(B1), .out(multiplier_1_out));  // open: cin, cout
  Multiplier #(.width(16)) multiplier_2 (.a(A1), .b(B2), .out(multiplier_2_out));  // open: cin, cout
  Multiplier #(.width(16)) multiplier_3 (.a(A2), .b(B3), .out(multiplier_3_out));  // open: cin, cout
  Multiplier #(.width(16)) multiplier_4 (.a(A2), .b(B4), .out(multiplier_4_out));  // open: cin, cout
  Multiplier #(.width(16)) multiplier_5 (.a(A3), .b(B1), .out(multiplier_5_out));  // open: cin, cout
  Multiplier #(.width(16)) multiplier_6 (.a(A4), .b(B3), .out(multiplier_6_out));  // open: cin, cout
  Multiplier #(.width(16)) multiplier_7 (.a(A3), .b(B2), .out(multiplier_7_out));  // open: cin, cout
  Multiplier #(.width(16)) multiplier_8 (.a(A4), .b(B4), .out(multiplier_8_out));  // open: cin, cout
  Adder #(.width(16)) adder_1 (.a(multiplier_5_out), .b(multiplier_6_out), .out(C));  // open: cin, cout
  Adder #(.width(16)) adder_2 (.a(multiplier_7_out), .b(multiplier_8_out), .out(D));  // open: cin, cout
  Adder #(.width(16)) adder_3 (.a(multiplier_1_out), .b(multiplier_3_out), .out(A));  // open: cin, cout
  Adder #(.width(16)) adder_4 (.a(multiplier_2_out), .b(multiplier_4_out), .out(B));  // open: cin, cout
endmodule

module Adder_2x2 (
  input  [15:0] A,
  input  [15:0] A1,
  input  [15:0] B,
  input  [15:0] B1,
  input  [15:0] C,
  input  [15:0] C1,
  input  [15:0] D,
  input  [15:0] D1,
  output [15:0] out_9,
  output [15:0] out_10,
  output [15:0] out_11,
  output [15:0] out_12
);

  Adder #(.width(16)) adder_1 (.a(A), .b(A1), .out(out_9));  // open: cin, cout
  Adder #(.width(16)) adder_2 (.a(B), .b(B1), .out(out_10));  // open: cin, cout
  Adder #(.width(16)) adder_3 (.a(C), .b(C1), .out(out_11));  // open: cin, cout
  Adder #(.width(16)) adder_4 (.a(D), .b(D1), .out(out_12));  // open: cin, cout
endmodule

module systolic_2x2 (
);

  wire clock_1_out, systollic_2_p7, systollic_3_p7, undriven, undriven_2, undriven_3, undriven_4, undriven_5;
  wire [7:0] counter_1_q, counter_2_q, counter_3_q, counter_4_q, counter_5_q, counter_6_q;
  wire [15:0] ram_1_dout, ram_2_dout, ram_3_dout, ram_4_dout, rom_1_data, systollic_1_aout, systollic_1_bout,
       systollic_1_sum_out;

  Clock clock_1 (.out(clock_1_out));
  RAM #(.dataWidth(16), .\type ("nonvolatile")) ram_1 (
    .addr(counter_1_q), .clk(clock_1_out), .dout(ram_1_dout));  // open: we, oe, din
  Counter counter_1 (.Q(counter_1_q), .up(1'b1), .clk(clock_1_out));  // open: load, D, count, carry, clr
  RAM #(.dataWidth(16), .\type ("nonvolatile")) ram_2 (
    .addr(counter_2_q), .clk(clock_1_out), .dout(ram_2_dout));  // open: we, oe, din
  Counter counter_2 (.Q(counter_2_q), .up(1'b1), .clk(clock_1_out));  // open: load, D, count, carry, clr
  Counter counter_3 (.Q(counter_3_q), .up(1'b1), .clk(clock_1_out));  // open: load, D, count, carry, clr
  RAM #(.dataWidth(16), .\type ("nonvolatile")) ram_3 (
    .addr(counter_3_q), .clk(clock_1_out), .dout(ram_3_dout));  // open: we, oe, din
  systollic systollic_1 (
    .sumIN(systollic_1_sum_out), .A(ram_1_dout), .B(ram_3_dout), .we(clock_1_out),
    .SUm_out(systollic_1_sum_out), .Aout(systollic_1_aout), .bout(systollic_1_bout));
  Counter counter_4 (.Q(counter_4_q), .up(1'b1), .clk(clock_1_out));  // open: load, D, count, carry, clr
  // systollic systollic_2: pin names not known; wires that end beside it: systollic_1_sum_out, ram_2_dout, systollic_1_bout, clock_1_out, rom_1_data[4], systollic_1_sum_out, systollic_2_p7
  RAM #(.dataWidth(16), .\type ("nonvolatile")) ram_4 (
    .addr(counter_4_q), .clk(clock_1_out), .dout(ram_4_dout));  // open: we, oe, din
  // systollic systollic_3: pin names not known; wires that end beside it: systollic_1_sum_out, systollic_1_aout, ram_4_dout, clock_1_out, rom_1_data[8], systollic_1_sum_out, systollic_3_p7
  // systollic systollic_4: pin names not known; wires that end beside it: systollic_1_sum_out, systollic_2_p7, systollic_3_p7, clock_1_out, rom_1_data[12], systollic_1_sum_out
  Counter counter_5 (.Q(counter_5_q), .up(1'b1), .clk(clock_1_out));  // open: load, D, count, carry, clr
  ROM #(.dataWidth(16)) rom_1 (.addr(counter_5_q), .data(rom_1_data));
  assign systollic_1_sum_out = undriven_2 ? systollic_1_sum_out : 16'bz;  // Controlled_Buffer controlled_buffer_1
  assign systollic_1_sum_out = undriven ? systollic_1_sum_out : 16'bz;  // Controlled_Buffer controlled_buffer_2
  assign systollic_1_sum_out = undriven_3 ? systollic_1_sum_out : 16'bz;  // Controlled_Buffer controlled_buffer_3
  assign systollic_1_sum_out = undriven_4 ? systollic_1_sum_out : 16'bz;  // Controlled_Buffer controlled_buffer_4
  Counter counter_6 (.count(undriven_5), .Q(counter_6_q), .up(1'b1));  // open: load, D, carry, clk, clr
  RAM #(.dataWidth(16)) ram_5 (
    .addr(counter_6_q), .we(undriven_5), .clk(clock_1_out), .din(systollic_1_sum_out));  // open: oe, dout

  // Notes on the sheet:
  //   contents of rom_1 (hex, n*v repeats v):
  //   0 4*1111
endmodule

module MATMULT_RXC (
);

  wire clock_1_out, or_1_out, or_2_out;
  wire [7:0] counter_1_q, counter_2_q, counter_3_q, counter_4_q;
  wire [15:0] matmul_1_sum2, ram_1_dout, ram_2_dout, register_1_q, register_2_q, register_3_q, register_4_q,
       register_5_q, register_6_q, register_7_q, register_8_q, register_9_q, rom_1_data;

  or or_1 (or_1_out, rom_1_data[3], rom_1_data[2], rom_1_data[1], rom_1_data[0]);
  RAM #(.dataWidth(16), .\type ("nonvolatile")) ram_1 (
    .addr(counter_1_q), .oe(or_1_out), .clk(clock_1_out), .dout(ram_1_dout));  // open: we, din
  Counter counter_1 (.count(or_1_out), .Q(counter_1_q), .up(1'b1), .clk(clock_1_out));  // open: load, D, carry, clr
  Clock clock_1 (.out(clock_1_out));
  Register #(.width(16)) register_1 (
    .D(ram_1_dout), .en(rom_1_data[0]), .clk(clock_1_out), .Q(register_1_q));  // open: clr
  Register #(.width(16)) register_2 (
    .D(ram_1_dout), .en(rom_1_data[1]), .clk(clock_1_out), .Q(register_2_q));  // open: clr
  Register #(.width(16)) register_3 (
    .D(ram_1_dout), .en(rom_1_data[2]), .clk(clock_1_out), .Q(register_3_q));  // open: clr
  Register #(.width(16)) register_4 (
    .D(ram_1_dout), .en(rom_1_data[3]), .clk(clock_1_out), .Q(register_4_q));  // open: clr
  or or_2 (or_2_out, rom_1_data[7], rom_1_data[6], rom_1_data[5], rom_1_data[4]);
  RAM #(.dataWidth(16), .\type ("nonvolatile")) ram_2 (
    .addr(counter_2_q), .oe(or_2_out), .clk(clock_1_out), .dout(ram_2_dout));  // open: we, din
  Counter #(.max('hf)) counter_2 (
    .count(or_2_out), .Q(counter_2_q), .up(1'b1), .clk(clock_1_out));  // open: load, D, carry, clr
  Register #(.width(16)) register_5 (
    .D(ram_2_dout), .en(rom_1_data[4]), .clk(clock_1_out), .Q(register_5_q));  // open: clr
  Register #(.width(16)) register_6 (
    .D(ram_2_dout), .en(rom_1_data[5]), .clk(clock_1_out), .Q(register_6_q));  // open: clr
  Register #(.width(16)) register_7 (
    .D(ram_2_dout), .en(rom_1_data[6]), .clk(clock_1_out), .Q(register_7_q));  // open: clr
  Register #(.width(16)) register_8 (
    .D(ram_2_dout), .en(rom_1_data[7]), .clk(clock_1_out), .Q(register_8_q));  // open: clr
  matmul matmul_1 (
    .A(register_1_q), .A1(register_2_q), .B(register_5_q), .B1(register_6_q), .A2(register_3_q),
    .B2(register_7_q), .A3(register_4_q), .B3(register_8_q), .sum2(matmul_1_sum2));
  Register #(.width(16)) register_9 (
    .D(matmul_1_sum2), .en(rom_1_data[8]), .clk(clock_1_out), .Q(register_9_q));  // open: clr
  // Probe on register_9_q
  Counter counter_3 (
    .count(rom_1_data[9]), .Q(counter_3_q), .up(1'b1), .clk(clock_1_out));  // open: load, D, carry, clr
  Counter counter_4 (.Q(counter_4_q), .up(1'b1), .clk(clock_1_out));  // open: load, D, count, carry, clr
  RAM #(.dataWidth(16)) ram_3 (
    .addr(counter_3_q), .we(rom_1_data[9]), .clk(clock_1_out), .din(register_9_q));  // open: oe, dout
  RAM #(.dataWidth(16), .\type ("nonvolatile")) ram_4 (.addr(counter_3_q));  // open: we, oe, clk, din, dout
  ROM #(.dataWidth(16)) rom_1 (.addr(counter_4_q), .data(rom_1_data));
  Hex_Digit_Display hex_digit_display_1 (.value(counter_4_q[7:4]));  // open: dp
  Hex_Digit_Display hex_digit_display_2 (.value(counter_4_q[3:0]));  // open: dp
  // Probe on counter_4_q

  // Notes on the sheet:
  //   contents of rom_1 (hex, n*v repeats v):
  //   11 11 22 44 88 110 220 40 80 110 220 40 80 110 220 40 80 111 222 44 88 110 220 40 80 110 220 40 80
  //   110 220 40 80 111 222 44 88 110 220 40 80 110 220 40 80 110 220 40 80 111 222 44 88 110 220 40 80
  //   110 220 40 80 110 220 40 80 111 222 44 88 110 220 40 80 110 220 40 80 110 220 40 80
endmodule

module systollic4x4 (
  input  in_1
);

  wire clock_1_out, or_1_out;
  wire [7:0] counter_1_q, counter_2_q, counter_3_q, counter_4_q, counter_5_q, counter_6_q, counter_7_q,
       counter_8_q, counter_9_q, counter_10_q;
  wire [15:0] controlled_buffer_1_out, ram_1_dout, ram_2_dout, ram_3_dout, ram_4_dout, ram_5_dout,
       ram_6_dout, ram_7_dout, ram_8_dout, register_1_q, register_2_q, register_3_q, register_4_q,
       register_5_q, register_6_q, register_7_q, register_8_q, register_9_q, register_10_q, register_11_q,
       register_12_q, register_13_q, register_14_q, register_15_q, register_16_q, register_17_q,
       register_18_q, register_19_q, register_20_q, systollic_1_aout, systollic_1_bout, systollic_1_sum_out,
       systollic_2_bout, systollic_2_sum_out, systollic_3_aout, systollic_3_bout, systollic_3_sum_out,
       systollic_4_aout, systollic_4_sum_out, systollic_5_aout, systollic_5_bout, systollic_5_sum_out,
       systollic_6_aout, systollic_6_bout, systollic_6_sum_out, systollic_7_aout, systollic_7_bout,
       systollic_7_sum_out, systollic_8_aout, systollic_8_sum_out, systollic_9_aout, systollic_9_bout,
       systollic_9_sum_out, systollic_10_aout, systollic_10_bout, systollic_10_sum_out, systollic_11_aout,
       systollic_11_bout, systollic_11_sum_out, systollic_12_aout, systollic_12_sum_out, systollic_13_bout,
       systollic_13_sum_out, systollic_14_bout, systollic_14_sum_out, systollic_15_bout,
       systollic_15_sum_out, systollic_16_sum_out;
  wire [31:0] rom_1_data;

  Counter counter_1 (.Q(counter_1_q), .up(1'b1), .clk(clock_1_out));  // open: load, D, count, carry, clr
  Counter counter_2 (.Q(counter_2_q), .up(1'b1), .clk(clock_1_out));  // open: load, D, count, carry, clr
  RAM #(.dataWidth(16), .\type ("nonvolatile")) ram_1 (
    .addr(counter_3_q), .clk(clock_1_out), .dout(ram_1_dout));  // open: we, oe, din
  Counter counter_3 (.Q(counter_3_q), .up(1'b1), .clk(clock_1_out));  // open: load, D, count, carry, clr
  RAM #(.dataWidth(16), .\type ("nonvolatile")) ram_2 (
    .addr(counter_1_q), .clk(clock_1_out), .dout(ram_2_dout));  // open: we, oe, din
  RAM #(.dataWidth(16), .\type ("nonvolatile")) ram_3 (
    .addr(counter_4_q), .clk(clock_1_out), .dout(ram_3_dout));  // open: we, oe, din
  Counter counter_4 (.Q(counter_4_q), .up(1'b1), .clk(clock_1_out));  // open: load, D, count, carry, clr
  RAM #(.dataWidth(16), .\type ("nonvolatile")) ram_4 (
    .addr(counter_2_q), .clk(clock_1_out), .dout(ram_4_dout));  // open: we, oe, din
  Clock clock_1 (.out(clock_1_out));
  Counter counter_5 (.Q(counter_5_q), .up(1'b1), .clk(clock_1_out));  // open: load, D, count, carry, clr
  Register #(.width(16)) register_1 (.D(ram_2_dout), .clk(clock_1_out), .Q(register_1_q));  // open: en, clr
  Register #(.width(16)) register_2 (.D(ram_3_dout), .clk(clock_1_out), .Q(register_2_q));  // open: en, clr
  Register #(.width(16)) register_3 (.D(ram_4_dout), .clk(clock_1_out), .Q(register_3_q));  // open: en, clr
  RAM #(.dataWidth(16), .\type ("nonvolatile")) ram_5 (
    .addr(counter_5_q), .clk(clock_1_out), .dout(ram_5_dout));  // open: we, oe, din
  Register #(.width(16)) register_4 (.D(ram_1_dout), .en(in_1), .clk(clock_1_out), .Q(register_4_q));  // open: clr
  Counter counter_6 (.Q(counter_6_q), .up(1'b1), .clk(clock_1_out));  // open: load, D, count, carry, clr
  systollic systollic_1 (
    .sumIN(systollic_1_sum_out), .A(register_4_q), .B(ram_5_dout), .SUm_out(systollic_1_sum_out),
    .Aout(systollic_1_aout), .bout(systollic_1_bout));  // open: we
  systollic systollic_2 (
    .sumIN(systollic_2_sum_out), .A(register_1_q), .B(systollic_1_bout), .SUm_out(systollic_2_sum_out),
    .bout(systollic_2_bout));  // open: we, Aout
  systollic systollic_3 (
    .sumIN(systollic_3_sum_out), .A(register_2_q), .B(systollic_2_bout), .SUm_out(systollic_3_sum_out),
    .Aout(systollic_3_aout), .bout(systollic_3_bout));  // open: we
  systollic systollic_4 (
    .sumIN(systollic_4_sum_out), .A(register_3_q), .B(systollic_3_bout), .SUm_out(systollic_4_sum_out),
    .Aout(systollic_4_aout));  // open: we, bout
  RAM #(.dataWidth(16), .\type ("nonvolatile")) ram_6 (
    .addr(counter_6_q), .clk(clock_1_out), .dout(ram_6_dout));  // open: we, oe, din
  Counter counter_7 (.Q(counter_7_q), .up(1'b1), .clk(clock_1_out));  // open: load, D, count, carry, clr
  systollic systollic_5 (
    .sumIN(systollic_5_sum_out), .A(systollic_1_aout), .B(ram_6_dout), .SUm_out(systollic_5_sum_out),
    .Aout(systollic_5_aout), .bout(systollic_5_bout));  // open: we
  systollic systollic_6 (
    .sumIN(systollic_6_sum_out), .B(systollic_5_bout), .SUm_out(systollic_6_sum_out),
    .Aout(systollic_6_aout), .bout(systollic_6_bout));  // open: A, we
  systollic systollic_7 (
    .sumIN(systollic_7_sum_out), .A(systollic_3_aout), .B(systollic_6_bout), .SUm_out(systollic_7_sum_out),
    .Aout(systollic_7_aout), .bout(systollic_7_bout));  // open: we
  systollic systollic_8 (
    .sumIN(systollic_8_sum_out), .A(systollic_4_aout), .B(systollic_7_bout), .SUm_out(systollic_8_sum_out),
    .Aout(systollic_8_aout));  // open: we, bout
  RAM #(.dataWidth(16), .\type ("nonvolatile")) ram_7 (
    .addr(counter_7_q), .clk(clock_1_out), .dout(ram_7_dout));  // open: we, oe, din
  RAM #(.dataWidth(16), .\type ("nonvolatile")) ram_8 (
    .addr(counter_8_q), .clk(clock_1_out), .dout(ram_8_dout));  // open: we, oe, din
  Counter counter_8 (.Q(counter_8_q), .up(1'b1), .clk(clock_1_out));  // open: load, D, count, carry, clr
  systollic systollic_9 (
    .sumIN(systollic_9_sum_out), .A(systollic_5_aout), .B(ram_7_dout), .SUm_out(systollic_9_sum_out),
    .Aout(systollic_9_aout), .bout(systollic_9_bout));  // open: we
  systollic systollic_10 (
    .sumIN(systollic_10_sum_out), .A(systollic_6_aout), .B(systollic_9_bout), .SUm_out(systollic_10_sum_out),
    .Aout(systollic_10_aout), .bout(systollic_10_bout));  // open: we
  systollic systollic_11 (
    .sumIN(systollic_11_sum_out), .A(systollic_7_aout), .B(systollic_10_bout),
    .SUm_out(systollic_11_sum_out), .Aout(systollic_11_aout), .bout(systollic_11_bout));  // open: we
  systollic systollic_12 (
    .sumIN(systollic_12_sum_out), .A(systollic_8_aout), .B(systollic_11_bout),
    .SUm_out(systollic_12_sum_out), .Aout(systollic_12_aout));  // open: we, bout
  systollic systollic_13 (
    .sumIN(systollic_13_sum_out), .A(systollic_9_aout), .B(ram_8_dout), .SUm_out(systollic_13_sum_out),
    .bout(systollic_13_bout));  // open: we, Aout
  systollic systollic_14 (
    .sumIN(systollic_14_sum_out), .A(systollic_10_aout), .B(systollic_13_bout),
    .SUm_out(systollic_14_sum_out), .bout(systollic_14_bout));  // open: we, Aout
  systollic systollic_15 (
    .sumIN(systollic_15_sum_out), .A(systollic_11_aout), .B(systollic_14_bout),
    .SUm_out(systollic_15_sum_out), .bout(systollic_15_bout));  // open: we, Aout
  systollic systollic_16 (
    .sumIN(systollic_16_sum_out), .A(systollic_12_aout), .B(systollic_15_bout), .SUm_out(systollic_16_sum_out));  // open: we, Aout, bout
  Register #(.width(16)) register_5 (
    .D(systollic_1_sum_out), .en(rom_1_data[0]), .clk(clock_1_out), .Q(register_5_q));  // open: clr
  Register #(.width(16)) register_6 (
    .D(systollic_5_sum_out), .en(rom_1_data[1]), .clk(clock_1_out), .Q(register_6_q));  // open: clr
  Register #(.width(16)) register_7 (
    .D(systollic_9_sum_out), .en(rom_1_data[2]), .clk(clock_1_out), .Q(register_7_q));  // open: clr
  Register #(.width(16)) register_8 (
    .D(systollic_13_sum_out), .en(rom_1_data[3]), .clk(clock_1_out), .Q(register_8_q));  // open: clr
  Register #(.width(16)) register_9 (
    .D(systollic_2_sum_out), .en(rom_1_data[4]), .clk(clock_1_out), .Q(register_9_q));  // open: clr
  Register #(.width(16)) register_10 (
    .D(systollic_6_sum_out), .en(rom_1_data[5]), .clk(clock_1_out), .Q(register_10_q));  // open: clr
  Register #(.width(16)) register_11 (
    .D(systollic_10_sum_out), .en(rom_1_data[6]), .clk(clock_1_out), .Q(register_11_q));  // open: clr
  Register #(.width(16)) register_12 (
    .D(systollic_14_sum_out), .en(rom_1_data[7]), .clk(clock_1_out), .Q(register_12_q));  // open: clr
  Counter counter_9 (.count(or_1_out), .Q(counter_9_q), .up(1'b1), .clk(clock_1_out));  // open: load, D, carry, clr
  Register #(.width(16)) register_13 (
    .D(systollic_3_sum_out), .en(rom_1_data[8]), .clk(clock_1_out), .Q(register_13_q));  // open: clr
  Register #(.width(16)) register_14 (
    .D(systollic_7_sum_out), .en(rom_1_data[9]), .clk(clock_1_out), .Q(register_14_q));  // open: clr
  Register #(.width(16)) register_15 (
    .D(systollic_11_sum_out), .en(rom_1_data[10]), .clk(clock_1_out), .Q(register_15_q));  // open: clr
  Register #(.width(16)) register_16 (
    .D(systollic_15_sum_out), .en(rom_1_data[11]), .clk(clock_1_out), .Q(register_16_q));  // open: clr
  Register #(.width(16)) register_17 (
    .D(systollic_4_sum_out), .en(rom_1_data[12]), .clk(clock_1_out), .Q(register_17_q));  // open: clr
  Register #(.width(16)) register_18 (
    .D(systollic_8_sum_out), .en(rom_1_data[13]), .clk(clock_1_out), .Q(register_18_q));  // open: clr
  Register #(.width(16)) register_19 (
    .D(systollic_11_bout), .en(rom_1_data[14]), .clk(clock_1_out), .Q(register_19_q));  // open: clr
  Register #(.width(16)) register_20 (
    .D(systollic_16_sum_out), .en(rom_1_data[15]), .clk(clock_1_out), .Q(register_20_q));  // open: clr
  Counter counter_10 (.Q(counter_10_q), .up(1'b1), .clk(clock_1_out));  // open: load, D, count, carry, clr
  assign controlled_buffer_1_out = rom_1_data[25] ? register_10_q : 16'bz;  // Controlled_Buffer controlled_buffer_1
  assign controlled_buffer_1_out = rom_1_data[31] ? register_8_q : 16'bz;  // Controlled_Buffer controlled_buffer_2
  assign controlled_buffer_1_out = rom_1_data[24] ? register_9_q : 16'bz;  // Controlled_Buffer controlled_buffer_3
  assign controlled_buffer_1_out = rom_1_data[29] ? register_6_q : 16'bz;  // Controlled_Buffer controlled_buffer_4
  assign controlled_buffer_1_out = rom_1_data[30] ? register_7_q : 16'bz;  // Controlled_Buffer controlled_buffer_5
  assign controlled_buffer_1_out = rom_1_data[28] ? register_5_q : 16'bz;  // Controlled_Buffer controlled_buffer_6
  assign controlled_buffer_1_out = rom_1_data[26] ? register_11_q : 16'bz;  // Controlled_Buffer controlled_buffer_7
  assign controlled_buffer_1_out = rom_1_data[20] ? register_13_q : 16'bz;  // Controlled_Buffer controlled_buffer_8
  assign controlled_buffer_1_out = rom_1_data[18] ? register_19_q : 16'bz;  // Controlled_Buffer controlled_buffer_9
  assign controlled_buffer_1_out = rom_1_data[19] ? register_20_q : 16'bz;  // Controlled_Buffer controlled_buffer_10
  assign controlled_buffer_1_out = rom_1_data[27] ? register_12_q : 16'bz;  // Controlled_Buffer controlled_buffer_11
  assign controlled_buffer_1_out = rom_1_data[21] ? register_14_q : 16'bz;  // Controlled_Buffer controlled_buffer_12
  assign controlled_buffer_1_out = rom_1_data[22] ? register_15_q : 16'bz;  // Controlled_Buffer controlled_buffer_13
  assign controlled_buffer_1_out = rom_1_data[23] ? register_16_q : 16'bz;  // Controlled_Buffer controlled_buffer_14
  assign controlled_buffer_1_out = rom_1_data[16] ? register_17_q : 16'bz;  // Controlled_Buffer controlled_buffer_15
  assign controlled_buffer_1_out = rom_1_data[17] ? register_18_q : 16'bz;  // Controlled_Buffer controlled_buffer_16
  RAM #(.dataWidth(16)) ram_9 (
    .addr(counter_9_q), .we(or_1_out), .clk(clock_1_out), .din(controlled_buffer_1_out));  // open: oe, dout
  or or_1 (or_1_out, rom_1_data[16], rom_1_data[17], rom_1_data[18], rom_1_data[19], rom_1_data[20], rom_1_data[21], rom_1_data[22], rom_1_data[23], rom_1_data[24], rom_1_data[25], rom_1_data[26], rom_1_data[27], rom_1_data[28], rom_1_data[29], rom_1_data[30], rom_1_data[31]);
  ROM #(.dataWidth(32)) rom_1 (.addr(counter_10_q), .data(rom_1_data));
endmodule

module core4x4 (
  input  [15:0] A1,
  input  [15:0] A2,
  input  [15:0] A3,
  input  [15:0] A4,
  input  [15:0] B1,
  input  [15:0] B5,
  input  [15:0] B9,
  input  [15:0] B13,
  input  [15:0] B2,
  input  [15:0] B6,
  input  [15:0] B10,
  input  [15:0] B14,
  input  [15:0] B3,
  input  [15:0] B7,
  input  [15:0] B11,
  input  [15:0] B15,
  input  [15:0] B4,
  input  [15:0] B8,
  input  [15:0] B12,
  input  [15:0] B16,
  input  [15:0] A5,
  input  [15:0] A6,
  input  [15:0] A7,
  input  [15:0] A8,
  input  [15:0] A9,
  input  [15:0] A10,
  input  [15:0] A11,
  input  [15:0] A12,
  input  [15:0] A13,
  input  [15:0] A14,
  input  [15:0] A15,
  input  [15:0] A16,
  input  [15:0] in_33,
  input  [15:0] in_34,
  input  [15:0] in_35,
  input  [15:0] in_36,
  input  [15:0] in_37,
  input  [15:0] in_38,
  input  [15:0] in_39,
  input  [15:0] in_40,
  input  [15:0] in_41,
  input  [15:0] in_42,
  input  [15:0] in_43,
  input  [15:0] in_44,
  input  [15:0] in_45,
  input  [15:0] in_46,
  input  [15:0] in_47,
  input  [15:0] in_48,
  output [15:0] C1,
  output [15:0] c2,
  output [15:0] c3,
  output [15:0] c4,
  output [15:0] c5,
  output [15:0] c6,
  output [15:0] c7,
  output [15:0] c8,
  output [15:0] c9,
  output [15:0] c10,
  output [15:0] c11,
  output [15:0] c12,
  output [15:0] c13,
  output [15:0] c14,
  output [15:0] c15,
  output [15:0] c16
);

  wire [15:0] adder_1_out, adder_2_out, adder_3_out, adder_4_out, adder_5_out, adder_6_out, adder_7_out,
       adder_8_out, adder_9_out, adder_10_out, adder_11_out, adder_12_out, adder_13_out, adder_14_out,
       adder_15_out, adder_16_out, adder_17_out, adder_18_out, adder_19_out, adder_20_out, adder_21_out,
       adder_22_out, adder_23_out, adder_24_out, adder_25_out, adder_26_out, adder_27_out, adder_28_out,
       adder_29_out, adder_30_out, adder_31_out, adder_32_out, adder_33_out, adder_34_out, adder_35_out,
       adder_36_out, adder_37_out, adder_38_out, adder_39_out, adder_40_out, adder_41_out, adder_42_out,
       adder_43_out, adder_44_out, adder_45_out, adder_46_out, adder_47_out, adder_48_out, multiplier_1_out,
       multiplier_2_out, multiplier_3_out, multiplier_4_out, multiplier_5_out, multiplier_6_out,
       multiplier_7_out, multiplier_8_out, multiplier_9_out, multiplier_10_out, multiplier_11_out,
       multiplier_12_out, multiplier_13_out, multiplier_14_out, multiplier_15_out, multiplier_16_out,
       multiplier_17_out, multiplier_18_out, multiplier_19_out, multiplier_20_out, multiplier_21_out,
       multiplier_22_out, multiplier_23_out, multiplier_24_out, multiplier_25_out, multiplier_26_out,
       multiplier_27_out, multiplier_28_out, multiplier_29_out, multiplier_30_out, multiplier_31_out,
       multiplier_32_out, multiplier_33_out, multiplier_34_out, multiplier_35_out, multiplier_36_out,
       multiplier_37_out, multiplier_38_out, multiplier_39_out, multiplier_40_out, multiplier_41_out,
       multiplier_42_out, multiplier_43_out, multiplier_44_out, multiplier_45_out, multiplier_46_out,
       multiplier_47_out, multiplier_48_out, multiplier_49_out, multiplier_50_out, multiplier_51_out,
       multiplier_52_out, multiplier_53_out, multiplier_54_out, multiplier_55_out, multiplier_56_out,
       multiplier_57_out, multiplier_58_out, multiplier_59_out, multiplier_60_out, multiplier_61_out,
       multiplier_62_out, multiplier_63_out, multiplier_64_out;

  Multiplier #(.width(16)) multiplier_1 (.a(A5), .b(B1), .out(multiplier_1_out));  // open: cin, cout
  Multiplier #(.width(16)) multiplier_2 (.a(A6), .b(B5), .out(multiplier_2_out));  // open: cin, cout
  Multiplier #(.width(16)) multiplier_3 (.a(A7), .b(B9), .out(multiplier_3_out));  // open: cin, cout
  Multiplier #(.width(16)) multiplier_4 (.a(A8), .b(B13), .out(multiplier_4_out));  // open: cin, cout
  Multiplier #(.width(16)) multiplier_5 (.a(B2), .b(A5), .out(multiplier_5_out));  // open: cin, cout
  Multiplier #(.width(16)) multiplier_6 (.a(A6), .b(B6), .out(multiplier_6_out));  // open: cin, cout
  Multiplier #(.width(16)) multiplier_7 (.a(B3), .b(A5), .out(multiplier_7_out));  // open: cin, cout
  Multiplier #(.width(16)) multiplier_8 (.a(B7), .b(A6), .out(multiplier_8_out));  // open: cin, cout
  Multiplier #(.width(16)) multiplier_9 (.a(B11), .b(A7), .out(multiplier_9_out));  // open: cin, cout
  Multiplier #(.width(16)) multiplier_10 (.a(B4), .b(A5), .out(multiplier_10_out));  // open: cin, cout
  Multiplier #(.width(16)) multiplier_11 (.a(A9), .b(B1), .out(multiplier_11_out));  // open: cin, cout
  Multiplier #(.width(16)) multiplier_12 (.a(A10), .b(B5), .out(multiplier_12_out));  // open: cin, cout
  Multiplier #(.width(16)) multiplier_13 (.a(A1), .b(B1), .out(multiplier_13_out));  // open: cin, cout
  Multiplier #(.width(16)) multiplier_14 (.a(A2), .b(B5), .out(multiplier_14_out));  // open: cin, cout
  Multiplier #(.width(16)) multiplier_15 (.a(A1), .b(B2), .out(multiplier_15_out));  // open: cin, cout
  Multiplier #(.width(16)) multiplier_16 (.a(A2), .b(B6), .out(multiplier_16_out));  // open: cin, cout
  Multiplier #(.width(16)) multiplier_17 (.a(A3), .b(B10), .out(multiplier_17_out));  // open: cin, cout
  Multiplier #(.width(16)) multiplier_18 (.a(A1), .b(B3), .out(multiplier_18_out));  // open: cin, cout
  Multiplier #(.width(16)) multiplier_19 (.a(A1), .b(B4), .out(multiplier_19_out));  // open: cin, cout
  Multiplier #(.width(16)) multiplier_20 (.a(A2), .b(B8), .out(multiplier_20_out));  // open: cin, cout
  Multiplier #(.width(16)) multiplier_21 (.a(A7), .b(B10), .out(multiplier_21_out));  // open: cin, cout
  Multiplier #(.width(16)) multiplier_22 (.a(A8), .b(B15), .out(multiplier_22_out));  // open: cin, cout
  Multiplier #(.width(16)) multiplier_23 (.a(B8), .b(A6), .out(multiplier_23_out));  // open: cin, cout
  Multiplier #(.width(16)) multiplier_24 (.a(A11), .b(B9), .out(multiplier_24_out));  // open: cin, cout
  Multiplier #(.width(16)) multiplier_25 (.a(A9), .b(B2), .out(multiplier_25_out));  // open: cin, cout
  Multiplier #(.width(16)) multiplier_26 (.a(A10), .b(B6), .out(multiplier_26_out));  // open: cin, cout
  Multiplier #(.width(16)) multiplier_27 (.a(A3), .b(B9), .out(multiplier_27_out));  // open: cin, cout
  Multiplier #(.width(16)) multiplier_28 (.a(B14), .b(A4), .out(multiplier_28_out));  // open: cin, cout
  Multiplier #(.width(16)) multiplier_29 (.a(A2), .b(B7), .out(multiplier_29_out));  // open: cin, cout
  Multiplier #(.width(16)) multiplier_30 (.a(A3), .b(B12), .out(multiplier_30_out));  // open: cin, cout
  Adder #(.width(16)) adder_1 (.a(multiplier_1_out), .b(multiplier_2_out), .out(adder_1_out));  // open: cin, cout
  Multiplier #(.width(16)) multiplier_31 (.a(A8), .b(B14), .out(multiplier_31_out));  // open: cin, cout
  Multiplier #(.width(16)) multiplier_32 (.a(B12), .b(A7), .out(multiplier_32_out));  // open: cin, cout
  Multiplier #(.width(16)) multiplier_33 (.a(B16), .b(A8), .out(multiplier_33_out));  // open: cin, cout
  Multiplier #(.width(16)) multiplier_34 (.a(A12), .b(B13), .out(multiplier_34_out));  // open: cin, cout
  Multiplier #(.width(16)) multiplier_35 (.a(A11), .b(B10), .out(multiplier_35_out));  // open: cin, cout
  Multiplier #(.width(16)) multiplier_36 (.a(A9), .b(B3), .out(multiplier_36_out));  // open: cin, cout
  Multiplier #(.width(16)) multiplier_37 (.a(A4), .b(B13), .out(multiplier_37_out));  // open: cin, cout
  Multiplier #(.width(16)) multiplier_38 (.a(A3), .b(B11), .out(multiplier_38_out));  // open: cin, cout
  Multiplier #(.width(16)) multiplier_39 (.a(A4), .b(B15), .out(multiplier_39_out));  // open: cin, cout
  Multiplier #(.width(16)) multiplier_40 (.a(A4), .b(B16), .out(multiplier_40_out));  // open: cin, cout
  Adder #(.width(16)) adder_2 (.a(multiplier_3_out), .b(multiplier_4_out), .out(adder_2_out));  // open: cin, cout
  Adder #(.width(16)) adder_3 (.a(multiplier_7_out), .b(multiplier_8_out), .out(adder_3_out));  // open: cin, cout
  Multiplier #(.width(16)) multiplier_41 (.a(B14), .b(A12), .out(multiplier_41_out));  // open: cin, cout
  Multiplier #(.width(16)) multiplier_42 (.a(A10), .b(B7), .out(multiplier_42_out));  // open: cin, cout
  Multiplier #(.width(16)) multiplier_43 (.a(A9), .b(B4), .out(multiplier_43_out));  // open: cin, cout
  Multiplier #(.width(16)) multiplier_44 (.a(A13), .b(B1), .out(multiplier_44_out));  // open: cin, cout
  Adder #(.width(16)) adder_4 (.a(multiplier_15_out), .b(multiplier_16_out), .out(adder_4_out));  // open: cin, cout
  Adder #(.width(16)) adder_5 (.a(multiplier_5_out), .b(multiplier_6_out), .out(adder_5_out));  // open: cin, cout
  Adder #(.width(16)) adder_6 (.a(multiplier_9_out), .b(multiplier_22_out), .out(adder_6_out));  // open: cin, cout
  Adder #(.width(16)) adder_7 (.a(multiplier_10_out), .b(multiplier_23_out), .out(adder_7_out));  // open: cin, cout
  Adder #(.width(16)) adder_8 (.a(multiplier_11_out), .b(multiplier_12_out), .out(adder_8_out));  // open: cin, cout
  Multiplier #(.width(16)) multiplier_45 (.a(A11), .b(B11), .out(multiplier_45_out));  // open: cin, cout
  Multiplier #(.width(16)) multiplier_46 (.a(B15), .b(A12), .out(multiplier_46_out));  // open: cin, cout
  Multiplier #(.width(16)) multiplier_47 (.a(A10), .b(B8), .out(multiplier_47_out));  // open: cin, cout
  Multiplier #(.width(16)) multiplier_48 (.a(B5), .b(A14), .out(multiplier_48_out));  // open: cin, cout
  Adder #(.width(16)) adder_9 (.a(multiplier_13_out), .b(multiplier_14_out), .out(adder_9_out));  // open: cin, cout
  Adder #(.width(16)) adder_10 (.a(multiplier_17_out), .b(multiplier_28_out), .out(adder_10_out));  // open: cin, cout
  Adder #(.width(16)) adder_11 (.a(multiplier_18_out), .b(multiplier_29_out), .out(adder_11_out));  // open: cin, cout
  Adder #(.width(16)) adder_12 (.a(multiplier_19_out), .b(multiplier_20_out), .out(adder_12_out));  // open: cin, cout
  Adder #(.width(16)) adder_13 (.a(multiplier_21_out), .b(multiplier_31_out), .out(adder_13_out));  // open: cin, cout
  Adder #(.width(16)) adder_14 (.a(multiplier_32_out), .b(multiplier_33_out), .out(adder_14_out));  // open: cin, cout
  Adder #(.width(16)) adder_15 (.a(multiplier_24_out), .b(multiplier_34_out), .out(adder_15_out));  // open: cin, cout
  Adder #(.width(16)) adder_16 (.a(multiplier_25_out), .b(multiplier_26_out), .out(adder_16_out));  // open: cin, cout
  Multiplier #(.width(16)) multiplier_49 (.a(A11), .b(B12), .out(multiplier_49_out));  // open: cin, cout
  Multiplier #(.width(16)) multiplier_50 (.a(B9), .b(A15), .out(multiplier_50_out));  // open: cin, cout
  Multiplier #(.width(16)) multiplier_51 (.a(A13), .b(B2), .out(multiplier_51_out));  // open: cin, cout
  Multiplier #(.width(16)) multiplier_52 (.a(A14), .b(B6), .out(multiplier_52_out));  // open: cin, cout
  Adder #(.width(16)) adder_17 (.a(multiplier_27_out), .b(multiplier_37_out), .out(adder_17_out));  // open: cin, cout
  Adder #(.width(16)) adder_18 (.a(multiplier_38_out), .b(multiplier_39_out), .out(adder_18_out));  // open: cin, cout
  Adder #(.width(16)) adder_19 (.a(multiplier_30_out), .b(multiplier_40_out), .out(adder_19_out));  // open: cin, cout
  Adder #(.width(16)) adder_20 (.a(multiplier_35_out), .b(multiplier_41_out), .out(adder_20_out));  // open: cin, cout
  Adder #(.width(16)) adder_21 (.a(multiplier_36_out), .b(multiplier_42_out), .out(adder_21_out));  // open: cin, cout
  Multiplier #(.width(16)) multiplier_53 (.a(B16), .b(A12), .out(multiplier_53_out));  // open: cin, cout
  Multiplier #(.width(16)) multiplier_54 (.a(B13), .b(A16), .out(multiplier_54_out));  // open: cin, cout
  Multiplier #(.width(16)) multiplier_55 (.a(B10), .b(A15), .out(multiplier_55_out));  // open: cin, cout
  Multiplier #(.width(16)) multiplier_56 (.a(A13), .b(B3), .out(multiplier_56_out));  // open: cin, cout
  Multiplier #(.width(16)) multiplier_57 (.a(A14), .b(B7), .out(multiplier_57_out));  // open: cin, cout
  Adder #(.width(16)) adder_22 (.a(adder_1_out), .b(adder_2_out), .out(adder_22_out));  // open: cin, cout
  Adder #(.width(16)) adder_23 (.a(adder_3_out), .b(adder_6_out), .out(adder_23_out));  // open: cin, cout
  Adder #(.width(16)) adder_24 (.a(multiplier_45_out), .b(multiplier_46_out), .out(adder_24_out));  // open: cin, cout
  Adder #(.width(16)) adder_25 (.a(multiplier_43_out), .b(multiplier_47_out), .out(adder_25_out));  // open: cin, cout
  Multiplier #(.width(16)) multiplier_58 (.a(B14), .b(A16), .out(multiplier_58_out));  // open: cin, cout
  Multiplier #(.width(16)) multiplier_59 (.a(B11), .b(A15), .out(multiplier_59_out));  // open: cin, cout
  Multiplier #(.width(16)) multiplier_60 (.a(A13), .b(B4), .out(multiplier_60_out));  // open: cin, cout
  Multiplier #(.width(16)) multiplier_61 (.a(A14), .b(B8), .out(multiplier_61_out));  // open: cin, cout
  Adder #(.width(16)) adder_26 (.a(adder_4_out), .b(adder_10_out), .out(adder_26_out));  // open: cin, cout
  Adder #(.width(16)) adder_27 (.a(multiplier_49_out), .b(multiplier_53_out), .out(adder_27_out));  // open: cin, cout
  Adder #(.width(16)) adder_28 (.a(multiplier_44_out), .b(multiplier_48_out), .out(adder_28_out));  // open: cin, cout
  Multiplier #(.width(16)) multiplier_62 (.a(B15), .b(A16), .out(multiplier_62_out));  // open: cin, cout
  Adder #(.width(16)) adder_29 (.a(adder_5_out), .b(adder_13_out), .out(adder_29_out));  // open: cin, cout
  Adder #(.width(16)) adder_30 (.a(adder_7_out), .b(adder_14_out), .out(adder_30_out));  // open: cin, cout
  Adder #(.width(16)) adder_31 (.a(adder_8_out), .b(adder_15_out), .out(adder_31_out));  // open: cin, cout
  Adder #(.width(16)) adder_32 (.a(multiplier_50_out), .b(multiplier_54_out), .out(adder_32_out));  // open: cin, cout
  Adder #(.width(16)) adder_33 (.a(multiplier_51_out), .b(multiplier_52_out), .out(adder_33_out));  // open: cin, cout
  Multiplier #(.width(16)) multiplier_63 (.a(B12), .b(A15), .out(multiplier_63_out));  // open: cin, cout
  Multiplier #(.width(16)) multiplier_64 (.a(B16), .b(A16), .out(multiplier_64_out));  // open: cin, cout
  Adder #(.width(16)) adder_34 (.a(adder_9_out), .b(adder_17_out), .out(adder_34_out));  // open: cin, cout
  Adder #(.width(16)) adder_35 (.a(adder_11_out), .b(adder_18_out), .out(adder_35_out));  // open: cin, cout
  Adder #(.width(16)) adder_36 (.a(adder_12_out), .b(adder_19_out), .out(adder_36_out));  // open: cin, cout
  Adder #(.width(16)) adder_37 (.a(adder_16_out), .b(adder_20_out), .out(adder_37_out));  // open: cin, cout
  Adder #(.width(16)) adder_38 (.a(multiplier_55_out), .b(multiplier_58_out), .out(adder_38_out));  // open: cin, cout
  Adder #(.width(16)) adder_39 (.a(multiplier_56_out), .b(multiplier_57_out), .out(adder_39_out));  // open: cin, cout
  Adder #(.width(16)) adder_40 (.a(adder_21_out), .b(adder_24_out), .out(adder_40_out));  // open: cin, cout
  Adder #(.width(16)) adder_41 (.a(multiplier_59_out), .b(multiplier_62_out), .out(adder_41_out));  // open: cin, cout
  Adder #(.width(16)) adder_42 (.a(multiplier_60_out), .b(multiplier_61_out), .out(adder_42_out));  // open: cin, cout
  Adder #(.width(16)) adder_43 (.a(adder_25_out), .b(adder_27_out), .out(adder_43_out));  // open: cin, cout
  Adder #(.width(16)) adder_44 (.a(adder_28_out), .b(adder_32_out), .out(adder_44_out));  // open: cin, cout
  Adder #(.width(16)) adder_45 (.a(multiplier_63_out), .b(multiplier_64_out), .out(adder_45_out));  // open: cin, cout
  Adder #(.width(16)) adder_46 (.a(adder_33_out), .b(adder_38_out), .out(adder_46_out));  // open: cin, cout
  Adder #(.width(16)) adder_47 (.a(adder_39_out), .b(adder_41_out), .out(adder_47_out));  // open: cin, cout
  Adder #(.width(16)) adder_48 (.a(adder_42_out), .b(adder_45_out), .out(adder_48_out));  // open: cin, cout
  Adder #(.width(16)) adder_49 (.a(in_39), .b(adder_23_out), .out(c7));  // open: cin, cout
  Adder #(.width(16)) adder_50 (.a(in_33), .b(adder_34_out), .out(C1));  // open: cin, cout
  Adder #(.width(16)) adder_51 (.a(in_34), .b(adder_26_out), .out(c2));  // open: cin, cout
  Adder #(.width(16)) adder_52 (.a(in_35), .b(adder_35_out), .out(c3));  // open: cin, cout
  Adder #(.width(16)) adder_53 (.a(in_36), .b(adder_36_out), .out(c4));  // open: cin, cout
  Adder #(.width(16)) adder_54 (.a(in_37), .b(adder_22_out), .out(c5));  // open: cin, cout
  Adder #(.width(16)) adder_55 (.a(in_38), .b(adder_29_out), .out(c6));  // open: cin, cout
  Adder #(.width(16)) adder_56 (.a(in_40), .b(adder_30_out), .out(c8));  // open: cin, cout
  Adder #(.width(16)) adder_57 (.a(in_41), .b(adder_31_out), .out(c9));  // open: cin, cout
  Adder #(.width(16)) adder_58 (.a(in_42), .b(adder_37_out), .out(c10));  // open: cin, cout
  Adder #(.width(16)) adder_59 (.a(in_43), .b(adder_40_out), .out(c11));  // open: cin, cout
  Adder #(.width(16)) adder_60 (.a(in_44), .b(adder_43_out), .out(c12));  // open: cin, cout
  Adder #(.width(16)) adder_61 (.a(in_45), .b(adder_44_out), .out(c13));  // open: cin, cout
  Adder #(.width(16)) adder_62 (.a(in_46), .b(adder_46_out), .out(c14));  // open: cin, cout
  Adder #(.width(16)) adder_63 (.a(in_47), .b(adder_47_out), .out(c15));  // open: cin, cout
  Adder #(.width(16)) adder_64 (.a(in_48), .b(adder_48_out), .out(c16));  // open: cin, cout
endmodule

module Rxc_iram (
);

  wire and_1_out, and_2_out, clock_1_out, comparator_1_lt, comparator_2_lt, undriven;
  wire [3:0] counter_6_q, register_9_q, register_9_q_2;
  wire [7:0] counter_1_q, counter_2_q, counter_3_q, counter_4_q, counter_5_q, counter_7_q, subtractor_1_out;
  wire [15:0] inst_Ram_dout, matmul_1_sum2, ram_1_dout, ram_2_dout, register_1_q, register_2_q, register_3_q,
       register_4_q, register_5_q, register_6_q, register_7_q, register_8_q, register_10_q;
  wire [15:8] register_9_q_3;
  wire [31:0] rom_1_data;

  and and_1 (and_1_out, comparator_1_lt, register_9_q_3[12]);
  Clock clock_1 (.out(clock_1_out));
  Counter counter_1 (
    .count(and_1_out), .Q(counter_1_q), .clk(clock_1_out), .clr(rom_1_data[24]));  // open: load, D, carry, up
  RAM #(.dataWidth(16), .trigger("falling"), .\type ("nonvolatile")) ram_1 (
    .addr(counter_2_q), .oe(and_1_out), .clk(clock_1_out), .dout(ram_1_dout));  // open: we, din
  Counter #(.trigger("falling")) counter_2 (
    .D({register_9_q_2, register_9_q}), .count(and_1_out), .Q(counter_2_q), .clk(clock_1_out));  // open: load, carry, up, clr
  Counter counter_3 (
    .count(and_2_out), .Q(counter_3_q), .clk(clock_1_out), .clr(rom_1_data[25]));  // open: load, D, carry, up
  Register #(.width(16)) register_1 (
    .D(ram_1_dout), .en(rom_1_data[0]), .clk(clock_1_out), .Q(register_1_q));  // open: clr
  Register #(.width(16)) register_2 (
    .D(ram_1_dout), .en(rom_1_data[1]), .clk(clock_1_out), .Q(register_2_q));  // open: clr
  Register #(.width(16)) register_3 (
    .D(ram_1_dout), .en(rom_1_data[2]), .clk(clock_1_out), .Q(register_3_q));  // open: clr
  Register #(.width(16)) register_4 (
    .D(ram_1_dout), .en(rom_1_data[3]), .clk(clock_1_out), .Q(register_4_q));  // open: clr
  and and_2 (and_2_out, comparator_2_lt, register_9_q_3[13]);
  RAM #(.dataWidth(16), .trigger("falling"), .\type ("nonvolatile")) ram_2 (
    .addr(counter_4_q), .oe(and_2_out), .clk(clock_1_out), .dout(ram_2_dout));  // open: we, din
  Counter #(.max('hf), .trigger("falling")) counter_4 (
    .load(undriven), .D({register_9_q_2, register_9_q}), .count(and_2_out), .Q(counter_4_q), .clk(clock_1_out));  // open: carry, up, clr
  RAM #(.dataWidth(16), .\type ("nonvolatile")) inst_Ram (
    .addr(counter_5_q), .clk(clock_1_out), .dout(inst_Ram_dout));  // open: we, oe, din
  Counter counter_5 (
    .count(rom_1_data[12]), .Q(counter_5_q), .up(1'b1), .clk(clock_1_out));  // open: load, D, carry, clr
  Register #(.width(16)) register_5 (
    .D(ram_2_dout), .en(rom_1_data[4]), .clk(clock_1_out), .Q(register_5_q));  // open: clr
  Register #(.width(16)) register_6 (
    .D(ram_2_dout), .en(rom_1_data[5]), .clk(clock_1_out), .Q(register_6_q));  // open: clr
  Register #(.width(16)) register_7 (
    .D(ram_2_dout), .en(rom_1_data[6]), .clk(clock_1_out), .Q(register_7_q));  // open: clr
  Register #(.width(16)) register_8 (
    .D(ram_2_dout), .en(rom_1_data[7]), .clk(clock_1_out), .Q(register_8_q));  // open: clr
  Register #(.width(16)) register_9 (
    .D(inst_Ram_dout), .en(rom_1_data[13]), .clk(clock_1_out),
    .Q({register_9_q_3, register_9_q_2, register_9_q}));  // open: clr
  matmul matmul_1 (
    .A(register_1_q), .A1(register_2_q), .B(register_5_q), .B1(register_6_q), .A2(register_3_q),
    .B2(register_7_q), .A3(register_4_q), .B3(register_8_q), .sum2(matmul_1_sum2));
  Register #(.width(16)) register_10 (
    .D(matmul_1_sum2), .en(rom_1_data[8]), .clk(clock_1_out), .Q(register_10_q));  // open: clr
  Counter #(.max('hf), .width(4)) counter_6 (
    .Q(counter_6_q), .clk(clock_1_out), .clr(rom_1_data[28]));  // open: load, D, count, carry, up
  Subtractor subtractor_1 (.a({4'b0000, register_9_q_3[11:8]}), .b(8'h1), .out(subtractor_1_out));  // open: bin, bout
  // Probe on register_10_q
  Subtractor #(.width(1)) subtractor_2 (.a(1'b1));  // open: b, out, bin, bout
  Counter counter_7 (
    .count(rom_1_data[9]), .Q(counter_7_q), .up(1'b1), .clk(clock_1_out));  // open: load, D, carry, clr
  Comparator comparator_1 (.a(counter_1_q), .b(subtractor_1_out), .lt(comparator_1_lt));  // open: gt, eq
  RAM #(.dataWidth(16)) ram_3 (
    .addr(counter_7_q), .we(rom_1_data[9]), .clk(clock_1_out), .din(register_10_q));  // open: oe, dout
  RAM #(.dataWidth(16), .\type ("nonvolatile")) ram_4 (.addr(counter_7_q));  // open: we, oe, clk, din, dout
  ROM #(.dataWidth(32)) rom_1 (.addr({register_9_q_3[15:12], counter_6_q}), .data(rom_1_data));
  Comparator comparator_2 (.a(counter_3_q), .b(subtractor_1_out), .lt(comparator_2_lt));  // open: gt, eq

  // Notes on the sheet:
  //   contents of rom_1 (hex, n*v repeats v):
  //   1000 2000 14*0 1000 2000 1100001 100002 100004 100008 10000000 9*0 1000 2000 2200010 200020 200040
  //   200080 10000000 9*0 1000 2000 200 10000000 12*0 1000 2000 100 10000000
endmodule

module intruction_core (
  input  [15:0] in_1,
  output [3:0] opcode,
  output [3:0] dim,
  output [7:0] Adr
);


  assign Adr = in_1[7:0];
  assign dim = in_1[11:8];
  assign opcode = in_1[15:12];
endmodule

module tiling_Final (
);

  wire clock_1_out, comparator_1_eq, comparator_3_eq, loadA_tracker_p1, loadA_tracker_p5, or_1_out, or_2_out,
       or_3_out, or_4_out, or_5_out, or_6_out, or_7_out, or_8_out, or_9_out, or_10_out, or_11_out, or_12_out,
       or_13_out, or_14_out, or_15_out, or_16_out, or_17_out, or_18_out, or_19_out, or_20_out, or_21_out,
       or_22_out, or_23_out, or_24_out, or_25_out, or_26_out, or_27_out, or_28_out, or_29_out, or_30_out,
       or_31_out, or_32_out, or_33_out, or_34_out, or_35_out, or_36_out, or_37_out, or_38_out, or_39_out,
       or_40_out, or_41_out, or_42_out, or_43_out, or_44_out, undriven, undriven_2;
  wire [3:0] divider_1_out, loadA_tracker_p3, loadA_tracker_p4, loadB_Tracker_q, multiplier_1_out;
  wire [7:0] adder_1_out, controlled_buffer_1_out, controlled_buffer_2_out, controlled_buffer_14_out,
       counter_1_q, counter_2_q, counter_3_q, counter_4_q, counter_5_q, counter_6_q, counter_7_q,
       counter_8_q, counter_9_q, counter_10_q, counter_11_q, counter_12_q, counter_13_q, counter_14_q,
       counter_15_q, counter_16_q, counter_17_q, counter_18_q, counter_19_q, counter_20_q, counter_21_q,
       counter_22_q, counter_23_q, counter_24_q, counter_25_q, counter_26_q, counter_27_q, counter_28_q,
       counter_29_q, counter_30_q, counter_31_q, counter_32_q, counter_33_q, counter_34_q, counter_35_q,
       counter_36_q, counter_37_q, counter_38_q, counter_39_q, counter_40_q, counter_41_q,
       intruction_core_1_adr, subtractor_1_out;
  wire [15:0] A1_q, A2_q, A3_q, A4_q, A5_q, A6_q, A7_q, A8_q, A9_q, A10_q, A11_q, A12_q, A13_q, A14_q, A15_q,
       A16_q, B1_q, B2_q, B3_q, B4_q, B5_q, B6_q, B7_q, B8_q, B9_q, B10_q, B11_q, B12_q, B13_q, B14_q, B15_q,
       B16_q, controlled_buffer_3_out, controlled_buffer_6_out, controlled_buffer_11_out,
       controlled_buffer_17_out, controlled_buffer_21_out, core4x4_1_c1, core4x4_1_c2, core4x4_1_c3,
       core4x4_1_c4, core4x4_1_c5, core4x4_1_c6, core4x4_1_c7, core4x4_1_c8, core4x4_1_c9, core4x4_1_c10,
       core4x4_1_c11, core4x4_1_c12, core4x4_1_c13, core4x4_1_c14, core4x4_1_c15, core4x4_1_c16, I_RAM_dout,
       ram_1_dout, ram_2_dout, ram_3_dout, ram_4_dout, ram_5_dout, ram_6_dout, ram_7_dout, ram_8_dout,
       ram_9_dout, ram_10_dout, ram_11_dout, ram_12_dout, ram_13_dout, ram_14_dout, ram_15_dout, ram_16_dout,
       ram_17_dout, ram_18_dout, ram_19_dout, ram_20_dout, ram_21_dout, ram_22_dout, ram_23_dout,
       ram_24_dout, ram_25_dout, ram_26_dout, ram_27_dout, ram_28_dout, ram_29_dout, ram_30_dout,
       ram_31_dout, ram_32_dout, ram_33_dout, ram_34_dout, ram_35_dout, ram_36_dout, RAM_A_dout, RAM_B_dout,
       register_1_q, register_2_q, register_3_q, register_4_q, register_5_q, register_6_q, register_7_q,
       register_8_q, register_9_q, register_10_q, register_11_q, register_12_q, register_13_q, register_14_q,
       register_15_q, register_16_q, register_17_q;
  wire [15:8] intruction_core_1_dim;
  wire [63:0] rom_1_data, rom_2_data;

  or or_1 (or_1_out, rom_1_data[28], rom_1_data[32]);
  or or_2 (or_2_out, rom_1_data[12], rom_1_data[32]);
  or or_3 (or_3_out, rom_1_data[16], rom_1_data[32]);
  or or_4 (or_4_out, rom_1_data[20], rom_1_data[32]);
  or or_5 (or_5_out, rom_1_data[24], rom_1_data[32]);
  Counter counter_1 (
    .load(comparator_1_eq), .D(intruction_core_1_adr), .count(or_1_out), .Q(counter_1_q), .clk(clock_1_out),
    .clr(rom_1_data[34]));  // open: carry, up
  or or_6 (or_6_out, rom_1_data[0], rom_1_data[32]);
  or or_7 (or_7_out, rom_1_data[4], rom_1_data[32]);
  or or_8 (or_8_out, rom_1_data[8], rom_1_data[32]);
  Counter counter_2 (
    .load(or_35_out), .D(adder_1_out), .count(or_2_out), .Q(counter_2_q), .clk(clock_1_out),
    .clr(rom_1_data[34]));  // open: carry, up
  RAM #(.asyncread("true"), .dataWidth(16), .\type ("nonvolatile")) ram_1 (
    .addr(counter_4_q), .we(rom_1_data[16]), .oe(rom_1_data[32]), .clk(clock_1_out), .din(RAM_B_dout),
    .dout(ram_1_dout));
  RAM #(.asyncread("true"), .dataWidth(16), .\type ("nonvolatile")) ram_2 (
    .addr(counter_5_q), .we(rom_1_data[20]), .oe(rom_1_data[32]), .clk(clock_1_out), .din(RAM_B_dout),
    .dout(ram_2_dout));
  RAM #(.asyncread("true"), .dataWidth(16), .\type ("nonvolatile")) ram_3 (
    .addr(counter_6_q), .we(rom_1_data[24]), .oe(rom_1_data[32]), .clk(clock_1_out), .din(RAM_B_dout),
    .dout(ram_3_dout));
  RAM #(.asyncread("true"), .dataWidth(16), .\type ("nonvolatile")) ram_4 (
    .addr(counter_1_q), .we(rom_1_data[28]), .oe(rom_1_data[32]), .clk(clock_1_out), .din(RAM_B_dout),
    .dout(ram_4_dout));
  // Counter #(.max('hf), .width(4)) loadA_tracker: pin names not known; wires that end beside it: loadA_tracker_p1, loadA_tracker_p1, loadA_tracker_p3, loadA_tracker_p4, loadA_tracker_p5
  Counter counter_3 (
    .load(or_35_out), .D(adder_1_out), .count(or_6_out), .Q(counter_3_q), .clk(clock_1_out),
    .clr(rom_1_data[34]));  // open: carry, up
  RAM #(.asyncread("true"), .dataWidth(16), .\type ("nonvolatile")) ram_5 (
    .addr(counter_3_q), .we(rom_1_data[0]), .oe(rom_1_data[32]), .clk(clock_1_out), .din(RAM_A_dout),
    .dout(ram_5_dout));
  RAM #(.asyncread("true"), .dataWidth(16), .\type ("nonvolatile")) ram_6 (
    .addr(counter_7_q), .we(rom_1_data[4]), .oe(rom_1_data[32]), .clk(clock_1_out), .din(RAM_A_dout),
    .dout(ram_6_dout));
  RAM #(.asyncread("true"), .dataWidth(16), .\type ("nonvolatile")) ram_7 (
    .addr(counter_8_q), .we(rom_1_data[8]), .oe(rom_1_data[32]), .clk(clock_1_out), .din(RAM_A_dout),
    .dout(ram_7_dout));
  RAM #(.asyncread("true"), .dataWidth(16), .\type ("nonvolatile")) ram_8 (
    .addr(counter_2_q), .we(rom_1_data[12]), .oe(rom_1_data[32]), .clk(clock_1_out), .din(RAM_A_dout),
    .dout(ram_8_dout));
  Counter #(.max('hf), .width(4)) loadB_Tracker (
    .count(undriven), .Q(loadB_Tracker_q), .clk(undriven_2), .clr(comparator_3_eq));  // open: load, D, carry, up
  Counter counter_4 (
    .load(comparator_1_eq), .D(intruction_core_1_adr), .count(or_3_out), .Q(counter_4_q), .clk(clock_1_out),
    .clr(rom_1_data[34]));  // open: carry, up
  Counter counter_5 (
    .load(comparator_1_eq), .D(intruction_core_1_adr), .count(or_4_out), .Q(counter_5_q), .clk(clock_1_out),
    .clr(rom_1_data[34]));  // open: carry, up
  Counter counter_6 (
    .load(comparator_1_eq), .D(intruction_core_1_adr), .count(or_5_out), .Q(counter_6_q), .clk(clock_1_out),
    .clr(rom_1_data[34]));  // open: carry, up
  Counter counter_7 (
    .load(or_35_out), .D(adder_1_out), .count(or_7_out), .Q(counter_7_q), .clk(clock_1_out),
    .clr(rom_1_data[34]));  // open: carry, up
  Counter counter_8 (
    .load(or_35_out), .D(adder_1_out), .count(or_8_out), .Q(counter_8_q), .clk(clock_1_out),
    .clr(rom_1_data[34]));  // open: carry, up
  or or_9 (or_9_out, rom_1_data[32], rom_1_data[13]);
  or or_10 (or_10_out, rom_1_data[32], rom_1_data[29]);
  or or_11 (or_11_out, rom_1_data[32], rom_1_data[1]);
  or or_12 (or_12_out, rom_1_data[5], rom_1_data[32]);
  or or_13 (or_13_out, rom_1_data[32], rom_1_data[9]);
  Counter counter_9 (
    .load(or_35_out), .D(adder_1_out), .count(or_9_out), .Q(counter_9_q), .clk(clock_1_out),
    .clr(rom_1_data[34]));  // open: carry, up
  or or_14 (or_14_out, rom_1_data[32], rom_1_data[17]);
  RAM #(.asyncread("true"), .dataWidth(16), .\type ("nonvolatile")) ram_9 (
    .addr(counter_13_q), .we(rom_1_data[17]), .oe(rom_1_data[32]), .clk(clock_1_out), .din(RAM_B_dout),
    .dout(ram_9_dout));
  or or_15 (or_15_out, rom_1_data[21], rom_1_data[32]);
  RAM #(.asyncread("true"), .dataWidth(16), .\type ("nonvolatile")) ram_10 (
    .addr(counter_14_q), .we(rom_1_data[21]), .oe(rom_1_data[32]), .clk(clock_1_out), .din(RAM_B_dout),
    .dout(ram_10_dout));
  or or_16 (or_16_out, rom_1_data[32], rom_1_data[25]);
  RAM #(.asyncread("true"), .dataWidth(16), .\type ("nonvolatile")) ram_11 (
    .addr(counter_15_q), .we(rom_1_data[25]), .oe(rom_1_data[32]), .clk(clock_1_out), .din(RAM_B_dout),
    .dout(ram_11_dout));
  Counter counter_10 (
    .load(comparator_1_eq), .D(intruction_core_1_adr), .count(or_10_out), .Q(counter_10_q),
    .clk(clock_1_out), .clr(rom_1_data[34]));  // open: carry, up
  RAM #(.asyncread("true"), .dataWidth(16), .\type ("nonvolatile")) ram_12 (
    .addr(counter_10_q), .we(rom_1_data[29]), .oe(rom_1_data[32]), .clk(clock_1_out), .din(RAM_B_dout),
    .dout(ram_12_dout));
  RAM #(.asyncread("true"), .dataWidth(16), .\type ("nonvolatile")) ram_13 (
    .addr(counter_16_q), .we(rom_1_data[1]), .oe(rom_1_data[32]), .clk(clock_1_out), .din(RAM_A_dout),
    .dout(ram_13_dout));
  Counter counter_11 (
    .load(or_35_out), .D(adder_1_out), .count(or_12_out), .Q(counter_11_q), .clk(clock_1_out),
    .clr(rom_1_data[34]));  // open: carry, up
  RAM #(.asyncread("true"), .dataWidth(16), .\type ("nonvolatile")) ram_14 (
    .addr(counter_11_q), .we(rom_1_data[5]), .oe(rom_1_data[32]), .clk(clock_1_out), .din(RAM_A_dout),
    .dout(ram_14_dout));
  Counter counter_12 (
    .load(or_35_out), .D(adder_1_out), .count(or_13_out), .Q(counter_12_q), .clk(clock_1_out),
    .clr(rom_1_data[34]));  // open: carry, up
  RAM #(.asyncread("true"), .dataWidth(16), .\type ("nonvolatile")) ram_15 (
    .addr(counter_12_q), .we(rom_1_data[9]), .oe(rom_1_data[32]), .clk(clock_1_out), .din(RAM_A_dout),
    .dout(ram_15_dout));
  RAM #(.asyncread("true"), .dataWidth(16), .\type ("nonvolatile")) ram_16 (
    .addr(counter_9_q), .we(rom_1_data[13]), .oe(rom_1_data[32]), .clk(clock_1_out), .din(RAM_A_dout),
    .dout(ram_16_dout));
  Counter counter_13 (
    .load(comparator_1_eq), .D(intruction_core_1_adr), .count(or_14_out), .Q(counter_13_q),
    .clk(clock_1_out), .clr(rom_1_data[34]));  // open: carry, up
  Counter counter_14 (
    .load(comparator_1_eq), .D(intruction_core_1_adr), .count(or_15_out), .Q(counter_14_q),
    .clk(clock_1_out), .clr(rom_1_data[34]));  // open: carry, up
  Counter counter_15 (
    .load(comparator_1_eq), .D(intruction_core_1_adr), .count(or_16_out), .Q(counter_15_q),
    .clk(clock_1_out), .clr(rom_1_data[34]));  // open: carry, up
  Counter counter_16 (
    .load(or_35_out), .D(adder_1_out), .count(or_11_out), .Q(counter_16_q), .clk(clock_1_out),
    .clr(rom_1_data[34]));  // open: carry, up
  or or_17 (or_17_out, rom_1_data[30], rom_1_data[32]);
  or or_18 (or_18_out, rom_1_data[32], rom_1_data[10]);
  or or_19 (or_19_out, rom_1_data[14], rom_1_data[32]);
  Counter counter_17 (
    .load(comparator_1_eq), .D(intruction_core_1_adr), .count(or_20_out), .Q(counter_17_q),
    .clk(clock_1_out), .clr(rom_1_data[34]));  // open: carry, up
  or or_20 (or_20_out, rom_1_data[32], rom_1_data[26]);
  Counter counter_18 (
    .load(comparator_1_eq), .D(intruction_core_1_adr), .count(or_17_out), .Q(counter_18_q),
    .clk(clock_1_out), .clr(rom_1_data[34]));  // open: carry, up
  or or_21 (or_21_out, rom_1_data[32], rom_1_data[2]);
  or or_22 (or_22_out, rom_1_data[32], rom_1_data[6]);
  Counter counter_19 (
    .load(or_35_out), .D(adder_1_out), .count(or_18_out), .Q(counter_19_q), .clk(clock_1_out),
    .clr(rom_1_data[34]));  // open: carry, up
  Counter counter_20 (
    .load(or_35_out), .D(adder_1_out), .count(or_19_out), .Q(counter_20_q), .clk(clock_1_out),
    .clr(rom_1_data[34]));  // open: carry, up
  or or_23 (or_23_out, rom_1_data[32], rom_1_data[18]);
  RAM #(.asyncread("true"), .dataWidth(16), .\type ("nonvolatile")) ram_17 (
    .addr(counter_24_q), .we(rom_1_data[18]), .oe(rom_1_data[32]), .clk(clock_1_out), .din(RAM_B_dout),
    .dout(ram_17_dout));
  Counter counter_21 (
    .load(comparator_1_eq), .D(intruction_core_1_adr), .count(or_24_out), .Q(counter_21_q),
    .clk(clock_1_out), .clr(rom_1_data[34]));  // open: carry, up
  or or_24 (or_24_out, rom_1_data[32], rom_1_data[22]);
  RAM #(.asyncread("true"), .dataWidth(16), .\type ("nonvolatile")) ram_18 (
    .addr(counter_21_q), .we(rom_1_data[22]), .oe(rom_1_data[32]), .clk(clock_1_out), .din(RAM_B_dout),
    .dout(ram_18_dout));
  RAM #(.asyncread("true"), .dataWidth(16), .\type ("nonvolatile")) ram_19 (
    .addr(counter_17_q), .we(rom_1_data[26]), .oe(rom_1_data[32]), .clk(clock_1_out), .din(RAM_B_dout),
    .dout(ram_19_dout));
  RAM #(.asyncread("true"), .dataWidth(16), .\type ("nonvolatile")) ram_20 (
    .addr(counter_18_q), .we(rom_1_data[30]), .oe(rom_1_data[32]), .clk(clock_1_out), .din(RAM_B_dout),
    .dout(ram_20_dout));
  Counter counter_22 (
    .load(or_35_out), .D(adder_1_out), .count(or_21_out), .Q(counter_22_q), .clk(clock_1_out),
    .clr(rom_1_data[34]));  // open: carry, up
  RAM #(.asyncread("true"), .dataWidth(16), .\type ("nonvolatile")) ram_21 (
    .addr(counter_22_q), .we(rom_1_data[2]), .oe(rom_1_data[32]), .clk(clock_1_out), .din(RAM_A_dout),
    .dout(ram_21_dout));
  Counter counter_23 (
    .load(or_35_out), .D(adder_1_out), .count(or_22_out), .Q(counter_23_q), .clk(clock_1_out),
    .clr(rom_1_data[34]));  // open: carry, up
  RAM #(.asyncread("true"), .dataWidth(16), .\type ("nonvolatile")) ram_22 (
    .addr(counter_23_q), .we(rom_1_data[6]), .oe(rom_1_data[32]), .clk(clock_1_out), .din(RAM_A_dout),
    .dout(ram_22_dout));
  RAM #(.asyncread("true"), .dataWidth(16), .\type ("nonvolatile")) ram_23 (
    .addr(counter_19_q), .we(rom_1_data[10]), .oe(rom_1_data[32]), .clk(clock_1_out), .din(RAM_A_dout),
    .dout(ram_23_dout));
  RAM #(.asyncread("true"), .dataWidth(16), .\type ("nonvolatile")) ram_24 (
    .addr(counter_20_q), .we(rom_1_data[14]), .oe(rom_1_data[32]), .clk(clock_1_out), .din(RAM_A_dout),
    .dout(ram_24_dout));
  Counter counter_24 (
    .load(comparator_1_eq), .D(intruction_core_1_adr), .count(or_23_out), .Q(counter_24_q),
    .clk(clock_1_out), .clr(rom_1_data[34]));  // open: carry, up
  or or_25 (or_25_out, rom_1_data[11], rom_1_data[32]);
  or or_26 (or_26_out, rom_1_data[15], rom_1_data[32]);
  Counter counter_25 (
    .load(comparator_1_eq), .D(intruction_core_1_adr), .count(or_27_out), .Q(counter_25_q),
    .clk(clock_1_out), .clr(rom_1_data[34]));  // open: carry, up
  or or_27 (or_27_out, rom_1_data[27], rom_1_data[32]);
  or or_28 (or_28_out, rom_1_data[31], rom_1_data[32]);
  or or_29 (or_29_out, rom_1_data[32], rom_1_data[3]);
  or or_30 (or_30_out, rom_1_data[7], rom_1_data[32]);
  Counter counter_26 (
    .load(or_35_out), .D(adder_1_out), .count(or_25_out), .Q(counter_26_q), .clk(clock_1_out),
    .clr(rom_1_data[34]));  // open: carry, up
  Counter counter_27 (
    .load(or_35_out), .D(adder_1_out), .count(or_26_out), .Q(counter_27_q), .clk(clock_1_out),
    .clr(rom_1_data[34]));  // open: carry, up
  or or_31 (or_31_out, rom_1_data[32], rom_1_data[19]);
  RAM #(.asyncread("true"), .dataWidth(16), .\type ("nonvolatile")) ram_25 (
    .addr(counter_31_q), .we(rom_1_data[19]), .oe(rom_1_data[32]), .clk(clock_1_out), .din(RAM_B_dout),
    .dout(ram_25_dout));
  or or_32 (or_32_out, rom_1_data[23], rom_1_data[32]);
  RAM #(.asyncread("true"), .dataWidth(16), .\type ("nonvolatile")) ram_26 (
    .addr(counter_32_q), .we(rom_1_data[23]), .oe(rom_1_data[32]), .clk(clock_1_out), .din(RAM_B_dout),
    .dout(ram_26_dout));
  RAM #(.asyncread("true"), .dataWidth(16), .\type ("nonvolatile")) ram_27 (
    .addr(counter_25_q), .we(rom_1_data[27]), .oe(rom_1_data[32]), .clk(clock_1_out), .din(RAM_B_dout),
    .dout(ram_27_dout));
  Counter counter_28 (
    .load(comparator_1_eq), .D(intruction_core_1_adr), .count(or_28_out), .Q(counter_28_q),
    .clk(clock_1_out), .clr(rom_1_data[34]));  // open: carry, up
  Counter counter_29 (
    .load(or_35_out), .D(adder_1_out), .count(or_29_out), .Q(counter_29_q), .clk(clock_1_out),
    .clr(rom_1_data[34]));  // open: carry, up
  RAM #(.asyncread("true"), .dataWidth(16), .\type ("nonvolatile")) ram_28 (
    .addr(counter_29_q), .we(rom_1_data[3]), .oe(rom_1_data[32]), .clk(clock_1_out), .din(RAM_A_dout),
    .dout(ram_28_dout));
  Counter counter_30 (
    .load(or_35_out), .D(adder_1_out), .count(or_30_out), .Q(counter_30_q), .clk(clock_1_out),
    .clr(rom_1_data[34]));  // open: carry, up
  RAM #(.asyncread("true"), .dataWidth(16), .\type ("nonvolatile")) ram_29 (
    .addr(counter_30_q), .we(rom_1_data[7]), .oe(rom_1_data[32]), .clk(clock_1_out), .din(RAM_A_dout),
    .dout(ram_29_dout));
  RAM #(.asyncread("true"), .dataWidth(16), .\type ("nonvolatile")) ram_30 (
    .addr(counter_26_q), .we(rom_1_data[11]), .oe(rom_1_data[32]), .clk(clock_1_out), .din(RAM_A_dout),
    .dout(ram_30_dout));
  RAM #(.asyncread("true"), .dataWidth(16), .\type ("nonvolatile")) ram_31 (
    .addr(counter_27_q), .we(rom_1_data[15]), .oe(rom_1_data[32]), .clk(clock_1_out), .din(RAM_A_dout),
    .dout(ram_31_dout));
  Counter counter_31 (
    .load(comparator_1_eq), .D(intruction_core_1_adr), .count(or_31_out), .Q(counter_31_q),
    .clk(clock_1_out), .clr(rom_1_data[34]));  // open: carry, up
  Counter counter_32 (
    .load(comparator_1_eq), .D(intruction_core_1_adr), .count(or_32_out), .Q(counter_32_q),
    .clk(clock_1_out), .clr(rom_1_data[34]));  // open: carry, up
  RAM #(.asyncread("true"), .dataWidth(16), .\type ("nonvolatile")) ram_32 (
    .addr(counter_28_q), .we(rom_1_data[31]), .oe(rom_1_data[32]), .clk(clock_1_out), .din(RAM_B_dout),
    .dout(ram_32_dout));
  or or_33 (or_33_out, rom_1_data[0], rom_1_data[1], rom_1_data[2], rom_1_data[3], rom_1_data[4], rom_1_data[5], rom_1_data[6], rom_1_data[7], rom_1_data[8], rom_1_data[9], rom_1_data[10], rom_1_data[11], rom_1_data[12], rom_1_data[13], rom_1_data[14], rom_1_data[15]);
  assign controlled_buffer_1_out = rom_1_data[40] ? intruction_core_1_adr : 8'bz;  // Controlled_Buffer controlled_buffer_1
  Counter counter_33 (
    .load(rom_1_data[40]), .D(controlled_buffer_1_out), .count(or_33_out), .Q(counter_33_q), .clk(clock_1_out));  // open: carry, up, clr
  RAM #(.asyncread("true"), .dataWidth(16), .\type ("nonvolatile")) RAM_A (
    .addr(counter_33_q), .oe(or_33_out), .clk(clock_1_out), .dout(RAM_A_dout));  // open: we, din
  Counter A_tracker ();  // open: clr, load, up, count, clk, D, carry, Q
  Clock clock_1 (.out(clock_1_out));
  assign controlled_buffer_2_out = rom_1_data[39] ? intruction_core_1_adr : 8'bz;  // Controlled_Buffer controlled_buffer_2
  Counter counter_34 (
    .load(rom_1_data[39]), .D(controlled_buffer_2_out), .count(or_34_out), .Q(counter_34_q), .clk(clock_1_out));  // open: carry, up, clr
  RAM #(.asyncread("true"), .dataWidth(16), .\type ("nonvolatile")) RAM_B (
    .addr(counter_34_q), .oe(or_34_out), .clk(clock_1_out), .dout(RAM_B_dout));  // open: we, din
  or or_34 (or_34_out, rom_1_data[16], rom_1_data[17], rom_1_data[18], rom_1_data[19], rom_1_data[20], rom_1_data[21], rom_1_data[22], rom_1_data[23], rom_1_data[24], rom_1_data[25], rom_1_data[26], rom_1_data[27], rom_1_data[28], rom_1_data[29], rom_1_data[30], rom_1_data[31]);
  Counter B_tracker ();  // open: clr, load, up, count, clk, D, carry, Q
  Register #(.width(16)) A1 (.D(ram_5_dout), .en(rom_1_data[32]), .clk(clock_1_out), .Q(A1_q));  // open: clr
  Register #(.width(16)) A5 (.D(ram_6_dout), .en(rom_1_data[32]), .clk(clock_1_out), .Q(A5_q));  // open: clr
  Register #(.width(16)) A9 (.D(ram_7_dout), .en(rom_1_data[32]), .clk(clock_1_out), .Q(A9_q));  // open: clr
  Register #(.width(16)) B1 (.D(ram_1_dout), .en(rom_1_data[32]), .clk(clock_1_out), .Q(B1_q));  // open: clr
  Register #(.width(16)) B5 (.D(ram_2_dout), .en(rom_1_data[32]), .clk(clock_1_out), .Q(B5_q));  // open: clr
  Register #(.width(16)) B9 (.D(ram_3_dout), .en(rom_1_data[32]), .clk(clock_1_out), .Q(B9_q));  // open: clr
  Register #(.width(16)) A13 (.D(ram_8_dout), .en(rom_1_data[32]), .clk(clock_1_out), .Q(A13_q));  // open: clr
  Register #(.width(16)) B13 (.D(ram_4_dout), .en(rom_1_data[32]), .clk(clock_1_out), .Q(B13_q));  // open: clr
  Register #(.width(16)) A2 (.D(ram_13_dout), .en(rom_1_data[32]), .clk(clock_1_out), .Q(A2_q));  // open: clr
  Register #(.width(16)) A6 (.D(ram_14_dout), .en(rom_1_data[32]), .clk(clock_1_out), .Q(A6_q));  // open: clr
  Register #(.width(16)) A10 (.D(ram_15_dout), .en(rom_1_data[32]), .clk(clock_1_out), .Q(A10_q));  // open: clr
  Register #(.width(16)) A14 (.D(ram_16_dout), .en(rom_1_data[32]), .clk(clock_1_out), .Q(A14_q));  // open: clr
  Register #(.width(16)) B2 (.D(ram_9_dout), .en(rom_1_data[32]), .clk(clock_1_out), .Q(B2_q));  // open: clr
  Register #(.width(16)) B6 (.D(ram_10_dout), .en(rom_1_data[32]), .clk(clock_1_out), .Q(B6_q));  // open: clr
  Register #(.width(16)) B10 (.D(ram_11_dout), .en(rom_1_data[32]), .clk(clock_1_out), .Q(B10_q));  // open: clr
  Register #(.width(16)) B14 (.D(ram_12_dout), .en(rom_1_data[32]), .clk(clock_1_out), .Q(B14_q));  // open: clr
  Register #(.width(16)) A3 (.D(ram_21_dout), .en(rom_1_data[32]), .clk(clock_1_out), .Q(A3_q));  // open: clr
  Register #(.width(16)) A7 (.D(ram_22_dout), .en(rom_1_data[32]), .clk(clock_1_out), .Q(A7_q));  // open: clr
  Register #(.width(16)) A11 (.D(ram_23_dout), .en(rom_1_data[32]), .clk(clock_1_out), .Q(A11_q));  // open: clr
  Register #(.width(16)) A15 (.D(ram_24_dout), .en(rom_1_data[32]), .clk(clock_1_out), .Q(A15_q));  // open: clr
  Register #(.width(16)) B3 (.D(ram_17_dout), .en(rom_1_data[32]), .clk(clock_1_out), .Q(B3_q));  // open: clr
  Register #(.width(16)) B7 (.D(ram_18_dout), .en(rom_1_data[32]), .clk(clock_1_out), .Q(B7_q));  // open: clr
  Register #(.width(16)) B11 (.D(ram_19_dout), .en(rom_1_data[32]), .clk(clock_1_out), .Q(B11_q));  // open: clr
  Register #(.width(16)) B15 (.D(ram_20_dout), .en(rom_1_data[32]), .clk(clock_1_out), .Q(B15_q));  // open: clr
  Register #(.width(16)) A4 (.D(ram_28_dout), .en(rom_1_data[32]), .clk(clock_1_out), .Q(A4_q));  // open: clr
  Register #(.width(16)) A8 (.D(ram_29_dout), .en(rom_1_data[32]), .clk(clock_1_out), .Q(A8_q));  // open: clr
  Register #(.width(16)) A12 (.D(ram_30_dout), .en(rom_1_data[32]), .clk(clock_1_out), .Q(A12_q));  // open: clr
  Register #(.width(16)) A16 (.D(ram_31_dout), .en(rom_1_data[32]), .clk(clock_1_out), .Q(A16_q));  // open: clr
  Register #(.width(16)) B4 (.D(ram_25_dout), .en(rom_1_data[32]), .clk(clock_1_out), .Q(B4_q));  // open: clr
  Register #(.width(16)) B8 (.D(ram_26_dout), .en(rom_1_data[32]), .clk(clock_1_out), .Q(B8_q));  // open: clr
  Register #(.width(16)) B12 (.D(ram_27_dout), .en(rom_1_data[32]), .clk(clock_1_out), .Q(B12_q));  // open: clr
  Register #(.width(16)) B16 (.D(ram_32_dout), .en(rom_1_data[32]), .clk(clock_1_out), .Q(B16_q));  // open: clr
  // Probe on register_1_q
  core4x4 core4x4_1 (
    .A1(A1_q), .A2(A2_q), .A3(A3_q), .A4(A4_q), .B1(B1_q), .B5(B5_q), .B9(B9_q), .B13(B13_q), .B2(B2_q),
    .B6(B6_q), .B10(B10_q), .B14(B14_q), .B3(B3_q), .B7(B7_q), .B11(B11_q), .B15(B15_q), .B4(B4_q),
    .B8(B8_q), .B12(B12_q), .B16(B16_q), .A5(A5_q), .A6(A6_q), .A7(A7_q), .A8(A8_q), .A9(A9_q), .A10(A10_q),
    .A11(A11_q), .A12(A12_q), .A13(A13_q), .A14(A14_q), .A15(A15_q), .A16(A16_q), .in_33(register_1_q),
    .in_34(register_5_q), .in_35(register_9_q), .in_36(register_14_q), .in_37(register_2_q),
    .in_38(register_6_q), .in_39(register_10_q), .in_40(register_15_q), .in_41(register_3_q),
    .in_42(register_7_q), .in_43(register_11_q), .in_44(register_16_q), .in_45(register_4_q),
    .in_46(register_8_q), .in_47(register_12_q), .in_48(register_13_q), .C1(core4x4_1_c1), .c2(core4x4_1_c2),
    .c3(core4x4_1_c3), .c4(core4x4_1_c4), .c5(core4x4_1_c5), .c6(core4x4_1_c6), .c7(core4x4_1_c7),
    .c8(core4x4_1_c8), .c9(core4x4_1_c9), .c10(core4x4_1_c10), .c11(core4x4_1_c11), .c12(core4x4_1_c12),
    .c13(core4x4_1_c13), .c14(core4x4_1_c14), .c15(core4x4_1_c15), .c16(core4x4_1_c16));
  Register #(.width(16)) register_1 (
    .D(core4x4_1_c1), .en(rom_1_data[33]), .clk(clock_1_out), .Q(register_1_q), .clr(rom_1_data[35]));
  Register #(.width(16)) register_2 (
    .D(core4x4_1_c5), .en(rom_1_data[33]), .clk(clock_1_out), .Q(register_2_q), .clr(rom_1_data[35]));
  Register #(.width(16)) register_3 (
    .D(core4x4_1_c9), .en(rom_1_data[33]), .clk(clock_1_out), .Q(register_3_q), .clr(rom_1_data[35]));
  Register #(.width(16)) register_4 (
    .D(core4x4_1_c13), .en(rom_1_data[33]), .clk(clock_1_out), .Q(register_4_q), .clr(rom_1_data[35]));
  Register #(.width(16)) register_5 (
    .D(core4x4_1_c2), .en(rom_1_data[33]), .clk(clock_1_out), .Q(register_5_q), .clr(rom_1_data[35]));
  Register #(.width(16)) register_6 (
    .D(core4x4_1_c6), .en(rom_1_data[33]), .clk(clock_1_out), .Q(register_6_q), .clr(rom_1_data[35]));
  Register #(.width(16)) register_7 (
    .D(core4x4_1_c10), .en(rom_1_data[33]), .clk(clock_1_out), .Q(register_7_q), .clr(rom_1_data[35]));
  Register #(.width(16)) register_8 (
    .D(core4x4_1_c14), .en(rom_1_data[33]), .clk(clock_1_out), .Q(register_8_q), .clr(rom_1_data[35]));
  Register #(.width(16)) register_9 (
    .D(core4x4_1_c3), .en(rom_1_data[33]), .clk(clock_1_out), .Q(register_9_q), .clr(rom_1_data[35]));
  Register #(.width(16)) register_10 (
    .D(core4x4_1_c7), .en(rom_1_data[33]), .clk(clock_1_out), .Q(register_10_q), .clr(rom_1_data[35]));
  Register #(.width(16)) register_11 (
    .D(core4x4_1_c11), .en(rom_1_data[33]), .clk(clock_1_out), .Q(register_11_q), .clr(rom_1_data[35]));
  Register #(.width(16)) register_12 (
    .D(core4x4_1_c15), .en(rom_1_data[33]), .clk(clock_1_out), .Q(register_12_q), .clr(rom_1_data[35]));
  Register #(.width(16)) register_13 (
    .D(core4x4_1_c16), .en(rom_1_data[33]), .clk(clock_1_out), .Q(register_13_q), .clr(rom_1_data[35]));
  Register #(.width(16)) register_14 (
    .D(core4x4_1_c4), .en(rom_1_data[33]), .clk(clock_1_out), .Q(register_14_q), .clr(rom_1_data[35]));
  Register #(.width(16)) register_15 (
    .D(core4x4_1_c8), .en(rom_1_data[33]), .clk(clock_1_out), .Q(register_15_q), .clr(rom_1_data[35]));
  Register #(.width(16)) register_16 (
    .D(core4x4_1_c12), .en(rom_1_data[33]), .clk(clock_1_out), .Q(register_16_q), .clr(rom_1_data[35]));
  assign controlled_buffer_3_out = rom_1_data[61] ? register_8_q : 16'bz;  // Controlled_Buffer controlled_buffer_3
  assign controlled_buffer_3_out = rom_1_data[62] ? register_12_q : 16'bz;  // Controlled_Buffer controlled_buffer_4
  assign controlled_buffer_3_out = rom_1_data[63] ? register_13_q : 16'bz;  // Controlled_Buffer controlled_buffer_5
  or or_35 (or_35_out, rom_2_data[3], rom_2_data[7]);
  assign controlled_buffer_6_out = rom_1_data[48] ? register_1_q : 16'bz;  // Controlled_Buffer controlled_buffer_6
  assign controlled_buffer_6_out = rom_1_data[49] ? register_5_q : 16'bz;  // Controlled_Buffer controlled_buffer_7
  assign controlled_buffer_3_out = rom_1_data[60] ? register_4_q : 16'bz;  // Controlled_Buffer controlled_buffer_8
  Subtractor subtractor_1 (.a(counter_28_q), .b(intruction_core_1_adr), .out(subtractor_1_out));  // open: bin, bout
  assign controlled_buffer_6_out = rom_1_data[50] ? register_9_q : 16'bz;  // Controlled_Buffer controlled_buffer_9
  assign controlled_buffer_6_out = rom_1_data[51] ? register_14_q : 16'bz;  // Controlled_Buffer controlled_buffer_10
  assign controlled_buffer_11_out = rom_1_data[52] ? register_2_q : 16'bz;  // Controlled_Buffer controlled_buffer_11
  Comparator comparator_1 (.a(8'h3), .b(subtractor_1_out), .eq(comparator_1_eq));  // open: gt, lt
  assign controlled_buffer_11_out = rom_1_data[53] ? register_6_q : 16'bz;  // Controlled_Buffer controlled_buffer_12
  assign controlled_buffer_11_out = rom_1_data[54] ? register_10_q : 16'bz;  // Controlled_Buffer controlled_buffer_13
  Adder adder_1 (.a(intruction_core_1_adr), .b(controlled_buffer_14_out), .out(adder_1_out));  // open: cin, cout
  assign controlled_buffer_14_out = rom_2_data[3] ? {8{1'b0}} : 8'bz;  // Controlled_Buffer controlled_buffer_14
  assign controlled_buffer_14_out = rom_2_data[7] ? 8'h2 : 8'bz;  // Controlled_Buffer controlled_buffer_15
  assign controlled_buffer_11_out = rom_1_data[55] ? register_15_q : 16'bz;  // Controlled_Buffer controlled_buffer_16
  assign controlled_buffer_17_out = rom_1_data[56] ? register_3_q : 16'bz;  // Controlled_Buffer controlled_buffer_17
  assign controlled_buffer_17_out = rom_1_data[57] ? register_7_q : 16'bz;  // Controlled_Buffer controlled_buffer_18
  assign controlled_buffer_17_out = rom_1_data[58] ? register_11_q : 16'bz;  // Controlled_Buffer controlled_buffer_19
  assign controlled_buffer_17_out = rom_1_data[59] ? register_16_q : 16'bz;  // Controlled_Buffer controlled_buffer_20
  Counter counter_35 (.Q(counter_35_q), .clk(clock_1_out), .clr(rom_1_data[38]));  // open: load, D, count, carry, up
  ROM #(.addrWidth(16), .dataWidth(64)) rom_1 (.addr({intruction_core_1_dim, counter_35_q}), .data(rom_1_data));
  Counter counter_36 (.count(or_36_out), .Q(counter_36_q), .clk(clock_1_out));  // open: load, D, carry, up, clr
  RAM #(.dataWidth(16)) Result (
    .addr(counter_36_q), .we(or_36_out), .clk(clock_1_out), .din(controlled_buffer_21_out));  // open: oe, dout
  ROM #(.addrWidth(16), .dataWidth(64)) rom_2 (.addr({intruction_core_1_dim, counter_35_q}), .data(rom_2_data));
  Counter counter_37 (
    .count(rom_1_data[36]), .Q(counter_37_q), .up(1'b1), .clk(clock_1_out));  // open: load, D, carry, clr
  RAM #(.dataWidth(16), .\type ("nonvolatile")) I_RAM (
    .addr(counter_37_q), .clk(clock_1_out), .dout(I_RAM_dout));  // open: we, oe, din
  or or_36 (or_36_out, rom_2_data[0], rom_2_data[2], rom_2_data[4], rom_2_data[5]);
  Register #(.width(16)) register_17 (
    .D(I_RAM_dout), .en(rom_1_data[37]), .clk(clock_1_out), .Q(register_17_q));  // open: clr
  intruction_core intruction_core_1 (
    .in_1(register_17_q), .opcode(intruction_core_1_dim[15:12]), .dim(intruction_core_1_dim[11:8]),
    .Adr(intruction_core_1_adr));
  or or_37 (or_37_out, rom_1_data[48], rom_1_data[49], rom_1_data[50], rom_1_data[51]);
  or or_38 (or_38_out, rom_1_data[52], rom_1_data[53], rom_1_data[54], rom_1_data[55]);
  or or_39 (or_39_out, rom_1_data[56], rom_1_data[57], rom_1_data[58], rom_1_data[59]);
  or or_40 (or_40_out, rom_1_data[60], rom_1_data[61], rom_1_data[62], rom_1_data[63]);
  Comparator #(.width(4)) comparator_2 (
    .a(loadA_tracker_p3), .b(divider_1_out), .eq(loadA_tracker_p5));  // open: gt, lt
  Adder #(.width(4)) adder_2 (.a(divider_1_out), .b(4'b0001), .out(loadA_tracker_p4));  // open: cin, cout
  or or_41 (or_41_out, rom_2_data[0], or_37_out);
  or or_42 (or_42_out, rom_2_data[2], or_38_out);
  or or_43 (or_43_out, or_39_out, rom_2_data[4]);
  or or_44 (or_44_out, rom_2_data[5], or_40_out);
  Counter #(.max('hf)) counter_38 (
    .count(or_41_out), .Q(counter_38_q), .clk(clock_1_out), .clr(rom_2_data[1]));  // open: load, D, carry, up
  Counter #(.max('hf)) counter_39 (
    .count(or_42_out), .Q(counter_39_q), .clk(clock_1_out), .clr(rom_2_data[1]));  // open: load, D, carry, up
  Counter #(.max('hf)) counter_40 (
    .count(or_43_out), .Q(counter_40_q), .clk(clock_1_out), .clr(rom_2_data[1]));  // open: load, D, carry, up
  Counter #(.max('hf)) counter_41 (
    .count(or_44_out), .Q(counter_41_q), .clk(clock_1_out), .clr(rom_2_data[1]));  // open: load, D, carry, up
  Divider #(.width(4)) divider_1 (
    .a(intruction_core_1_dim[11:8]), .b(4'b0100), .out(divider_1_out));  // open: upper, rem
  RAM #(.asyncread("true"), .dataWidth(16), .\type ("nonvolatile")) ram_33 (
    .addr(counter_38_q), .we(or_37_out), .oe(rom_2_data[0]), .clk(clock_1_out),
    .din(controlled_buffer_6_out), .dout(ram_33_dout));
  RAM #(.asyncread("true"), .dataWidth(16), .\type ("nonvolatile")) ram_34 (
    .addr(counter_39_q), .we(or_38_out), .oe(rom_2_data[2]), .clk(clock_1_out),
    .din(controlled_buffer_11_out), .dout(ram_34_dout));
  RAM #(.asyncread("true"), .dataWidth(16), .\type ("nonvolatile")) ram_35 (
    .addr(counter_40_q), .we(or_39_out), .oe(rom_2_data[4]), .clk(clock_1_out),
    .din(controlled_buffer_17_out), .dout(ram_35_dout));
  RAM #(.asyncread("true"), .dataWidth(16), .\type ("nonvolatile")) ram_36 (
    .addr(counter_41_q), .we(or_40_out), .oe(rom_2_data[5]), .clk(clock_1_out),
    .din(controlled_buffer_3_out), .dout(ram_36_dout));
  Multiplier #(.width(4)) multiplier_1 (
    .a(divider_1_out), .b(divider_1_out), .out(multiplier_1_out));  // open: cin, cout
  Comparator #(.width(4)) comparator_3 (
    .a(loadB_Tracker_q), .b(multiplier_1_out), .eq(comparator_3_eq));  // open: gt, lt
  assign controlled_buffer_21_out = rom_2_data[6] ? ram_33_dout : 16'bz;  // Controlled_Buffer controlled_buffer_21
  assign controlled_buffer_21_out = rom_2_data[9] ? ram_35_dout : 16'bz;  // Controlled_Buffer controlled_buffer_22
  assign controlled_buffer_21_out = rom_2_data[8] ? ram_34_dout : 16'bz;  // Controlled_Buffer controlled_buffer_23
  assign controlled_buffer_21_out = rom_2_data[10] ? ram_36_dout : 16'bz;  // Controlled_Buffer controlled_buffer_24

  // Notes on the sheet:
  //   contents of rom_1 (hex, n*v repeats v):
  //   1000000000 2000000000 5118*0 1000000000 2000000000 1 2 4 8 10 20 40 80 100 200 400 800 1000 2000
  //   4000 8000 4000000000 1005*0 1000000000 2000000000 1 2 4 8 10 20 40 80 100 200 400 800 1000 2000 4000
  //   8000 1 2 4 8 10 20 40 80 100 200 400 800 1000 2000 4000 8000 1 2 4 8 10 20 40 80 100 200 400 800
  //   1000 2000 4000 8000 1 2 4 8 10 20 40 80 100 200 400 800 1000 2000 4000 8000 4000000000 3005*0
  //   1000000000 2000000000 10000 20000 40000 80000 100000 200000 400000 800000 1000000 2000000 4000000
  //   8000000 10000000 20000000 40000000 80000000 4000000000 1005*0 1000000000 2000000000 10000 20000
  //   40000 80000 100000 200000 400000 800000 1000000 2000000 4000000 8000000 10000000 20000000 40000000
  //   80000000 10000 20000 40000 80000 100000 200000 400000 800000 1000000 2000000 4000000 8000000
  //   10000000 20000000 40000000 80000000 10000 20000 40000 80000 100000 200000 400000 800000 1000000
  //   2000000 4000000 8000000 10000000 20000000 40000000 80000000 10000 20000 40000 80000 100000 200000
  //   400000 800000 1000000 2000000 4000000 8000000 10000000 20000000 40000000 80000000 4000000000 3012*0
  //   1000000000000 2000000000000 4000000000000 8000000000000 10000000000000 20000000000000 40000000000000
  //   80000000000000 100000000000000 20000000000000 400000000000000 800000000000000 1000000000000000
  //   2000000000000000 4000000000000000 8000000000000000 17*0 1000000000 2000000000 4056*0 400000000
  //   100000000 200000000 1000000000 2000000000 1019*0 400000000 300000000 300000000 300000000
  //   1000000000000 2000000000000 4000000000000 8000000000000 10000000000000 20000000000000 40000000000000
  //   80000000000000 100000000000000 200000000000000 400000000000000 800000000000000 1000000000000000
  //   2000000000000000 4000000000000000 8000000000000000 800000000 300000000 300000000 1000000000000
  //   300000000 300000000
  //   contents of rom_2 (hex, n*v repeats v):
  //   13335*0 2 4*41 4*104 4*210 4*420 5084*0 8
endmodule
